// Logisim project alu_test.circ as structural Verilog
module main (
  input  [4:0] in_1,
  input  [5:0] X,
  input  [5:0] Y,
  output [5:0] out_4,
  output ZF,
  output BAF,
  output INV_OP
);

  wire [8:0] ADD_z0, AND_z0, CMPZ_z0, DEC_s0, DIV_z0, INC_s0, INV_s0, MUL_z0, N0_z0, N1_z0, NEG_z0, NOT_z0,
       op1_z0, op2_z0, Op3_z0, OR_z0, ROL_z0, ROR_z0, SHL_s0, SHR_z0, SUB_z0, VLD_s0, XOR_z0;

  VLD VLD (
    .a5(X[5]), .a4(X[4]), .a3(X[3]), .a2(X[2]), .a1(X[1]), .a0(X[0]), .s5(VLD_s0[5]), .s4(VLD_s0[4]),
    .s3(VLD_s0[3]), .s2(VLD_s0[2]), .s1(VLD_s0[1]), .s0(VLD_s0[0]), .ZF(VLD_s0[6]), .BAF(VLD_s0[7]),
    .INV_OP(VLD_s0[8]));
  NEG2 NEG (
    .x5(X[5]), .x4(X[4]), .x3(X[3]), .x2(X[2]), .x1(X[1]), .x0(X[0]), .z5(NEG_z0[5]), .z4(NEG_z0[4]),
    .z3(NEG_z0[3]), .z2(NEG_z0[2]), .z1(NEG_z0[1]), .z0(NEG_z0[0]), .ZF(NEG_z0[6]), .BAF(NEG_z0[7]),
    .INV_OP(NEG_z0[8]));
  INC INC (
    .x5(X[5]), .x4(X[4]), .x3(X[3]), .x2(X[2]), .x1(X[1]), .x0(X[0]), .s5(INC_s0[5]), .s4(INC_s0[4]),
    .s3(INC_s0[3]), .s2(INC_s0[2]), .s1(INC_s0[1]), .s0(INC_s0[0]), .ZF(INC_s0[6]), .BAF(INC_s0[7]),
    .INV_OP(INC_s0[8]));
  DEC DEC (
    .x5(X[5]), .x4(X[4]), .x3(X[3]), .x2(X[2]), .x1(X[1]), .x0(X[0]), .s5(DEC_s0[5]), .s4(DEC_s0[4]),
    .s3(DEC_s0[3]), .s2(DEC_s0[2]), .s1(DEC_s0[1]), .s0(DEC_s0[0]), .ZF(DEC_s0[6]), .BAF(DEC_s0[7]),
    .INV_OP(DEC_s0[8]));
  CMPZ CMPZ (
    .x5(X[5]), .x4(X[4]), .x3(X[3]), .x2(X[2]), .x1(X[1]), .x0(X[0]), .z5(CMPZ_z0[5]), .z4(CMPZ_z0[4]),
    .z3(CMPZ_z0[3]), .z2(CMPZ_z0[2]), .z1(CMPZ_z0[1]), .z0(CMPZ_z0[0]), .ZF(CMPZ_z0[6]), .BAF(CMPZ_z0[7]),
    .INV_OP(CMPZ_z0[8]));
  INV INV (
    .x5(X[5]), .x4(X[4]), .x3(X[3]), .x2(X[2]), .x1(X[1]), .x0(X[0]), .s5(INV_s0[5]), .s4(INV_s0[4]),
    .s3(INV_s0[3]), .s2(INV_s0[2]), .s1(INV_s0[1]), .s0(INV_s0[0]), .ZF(INV_s0[6]), .BAF(INV_s0[7]),
    .INV_OP(INV_s0[8]));
  SHL SHL (
    .x5(X[5]), .x4(X[4]), .x3(X[3]), .x2(X[2]), .x1(X[1]), .x0(X[0]), .s5(SHL_s0[5]), .s4(SHL_s0[4]),
    .s3(SHL_s0[3]), .s2(SHL_s0[2]), .s1(SHL_s0[1]), .s0(SHL_s0[0]), .ZF(SHL_s0[6]), .BAF(SHL_s0[7]),
    .INV_OP(SHL_s0[8]));
  SHR SHR (
    .x5(X[5]), .x4(X[4]), .x3(X[3]), .x2(X[2]), .x1(X[1]), .x0(X[0]), .z5(SHR_z0[5]), .z4(SHR_z0[4]),
    .z3(SHR_z0[3]), .z2(SHR_z0[2]), .z1(SHR_z0[1]), .z0(SHR_z0[0]), .ZF(SHR_z0[6]), .BAF(SHR_z0[7]),
    .INV_OP(SHR_z0[8]));
  ROL ROL (
    .x5(X[5]), .x4(X[4]), .x3(X[3]), .x2(X[2]), .x1(X[1]), .x0(X[0]), .z5(ROL_z0[5]), .z4(ROL_z0[4]),
    .z3(ROL_z0[3]), .z2(ROL_z0[2]), .z1(ROL_z0[1]), .z0(ROL_z0[0]), .ZF(ROL_z0[6]), .BAF(ROL_z0[7]),
    .INV_OP(ROL_z0[8]));
  ROR ROR (
    .x5(X[5]), .x4(X[4]), .x3(X[3]), .x2(X[2]), .x1(X[1]), .x0(X[0]), .z5(ROR_z0[5]), .z4(ROR_z0[4]),
    .z3(ROR_z0[3]), .z2(ROR_z0[2]), .z1(ROR_z0[1]), .z0(ROR_z0[0]), .ZF(ROR_z0[6]), .BAF(ROR_z0[7]),
    .INV_OP(ROR_z0[8]));
  NOT NOT (
    .x0(X[0]), .x1(X[1]), .x2(X[2]), .x3(X[3]), .x4(X[4]), .x5(X[5]), .ZF(NOT_z0[7]), .z0(NOT_z0[0]),
    .z1(NOT_z0[1]), .z2(NOT_z0[2]), .z3(NOT_z0[3]), .z4(NOT_z0[4]), .z5(NOT_z0[5]), .BAF(NOT_z0[6]),
    .INV_OP(NOT_z0[8]));
  N1 N1 (
    .x5(X[5]), .x4(X[4]), .x3(X[3]), .x2(X[2]), .x1(X[1]), .x0(X[0]), .z5(N1_z0[5]), .z4(N1_z0[4]),
    .z3(N1_z0[3]), .z2(N1_z0[2]), .z1(N1_z0[1]), .z0(N1_z0[0]), .ZF(N1_z0[6]), .BAF(N1_z0[7]),
    .INV_OP(N1_z0[8]));
  N0 N0 (
    .x5(X[5]), .x4(X[4]), .x3(X[3]), .x2(X[2]), .x1(X[1]), .x0(X[0]), .z5(N0_z0[5]), .z4(N0_z0[4]),
    .z3(N0_z0[3]), .z2(N0_z0[2]), .z1(N0_z0[1]), .z0(N0_z0[0]), .ZF(N0_z0[6]), .BAF(N0_z0[7]),
    .INV_OP(N0_z0[8]));
  ADD ADD (
    .x0(X[0]), .x1(X[1]), .x2(X[2]), .x3(X[3]), .x4(X[4]), .x5(X[5]), .y0(Y[0]), .y1(Y[1]), .y2(Y[2]),
    .y3(Y[3]), .y4(Y[4]), .y5(Y[5]), .ZF(ADD_z0[6]), .z0(ADD_z0[0]), .z1(ADD_z0[1]), .z2(ADD_z0[2]),
    .z3(ADD_z0[3]), .z4(ADD_z0[4]), .z5(ADD_z0[5]), .BAF(ADD_z0[7]), .INV_OP(ADD_z0[8]));
  SUB SUB (
    .x0(X[0]), .x1(X[1]), .x2(X[2]), .x3(X[3]), .x4(X[4]), .x5(X[5]), .y0(Y[0]), .y1(Y[1]), .y2(Y[2]),
    .y3(Y[3]), .y4(Y[4]), .y5(Y[5]), .ZF(SUB_z0[6]), .z0(SUB_z0[0]), .z1(SUB_z0[1]), .z2(SUB_z0[2]),
    .z3(SUB_z0[3]), .z4(SUB_z0[4]), .z5(SUB_z0[5]), .BAF(SUB_z0[7]), .INV_OP(SUB_z0[8]));
  MUL MUL (
    .x0(X[0]), .x1(X[1]), .x2(X[2]), .x3(X[3]), .x4(X[4]), .x5(X[5]), .y0(Y[0]), .y1(Y[1]), .y2(Y[2]),
    .y3(Y[3]), .y4(Y[4]), .y5(Y[5]), .ZF(MUL_z0[6]), .z0(MUL_z0[0]), .z1(MUL_z0[1]), .z2(MUL_z0[2]),
    .z3(MUL_z0[3]), .z4(MUL_z0[4]), .z5(MUL_z0[5]), .BAF(MUL_z0[7]), .INV_OP(MUL_z0[8]));
  DIV DIV (
    .x0(X[0]), .x1(X[1]), .x2(X[2]), .x3(X[3]), .x4(X[4]), .x5(X[5]), .y0(Y[0]), .y1(Y[1]), .y2(Y[2]),
    .y3(Y[3]), .y4(Y[4]), .y5(Y[5]), .ZF(DIV_z0[6]), .z0(DIV_z0[0]), .z1(DIV_z0[1]), .z2(DIV_z0[2]),
    .z3(DIV_z0[3]), .z4(DIV_z0[4]), .z5(DIV_z0[5]), .BAF(DIV_z0[7]), .INV_OP(DIV_z0[8]));
  op1 op1 (
    .x0(X[0]), .x1(X[1]), .x2(X[2]), .x3(X[3]), .x4(X[4]), .x5(X[5]), .y0(Y[0]), .y1(Y[1]), .y2(Y[2]),
    .y3(Y[3]), .y4(Y[4]), .y5(Y[5]), .z5(op1_z0[5]), .z4(op1_z0[4]), .z3(op1_z0[3]), .z2(op1_z0[2]),
    .z1(op1_z0[1]), .z0(op1_z0[0]), .ZF(op1_z0[6]), .BAF(op1_z0[7]), .INV_OP(op1_z0[8]));
  op22 op2 (
    .x0(X[0]), .x1(X[1]), .x2(X[2]), .x3(X[3]), .x4(X[4]), .x5(X[5]), .y0(Y[0]), .y1(Y[1]), .y2(Y[2]),
    .y3(Y[3]), .y4(Y[4]), .y5(Y[5]), .z5(op2_z0[5]), .z4(op2_z0[4]), .z3(op2_z0[3]), .z2(op2_z0[2]),
    .z1(op2_z0[1]), .z0(op2_z0[0]), .ZF(op2_z0[6]), .BAF(op2_z0[7]), .INV_OP(op2_z0[8]));
  op3 Op3 (
    .x0(X[0]), .x1(X[1]), .x2(X[2]), .x3(X[3]), .x4(X[4]), .x5(X[5]), .z0(Op3_z0[0]), .z1(Op3_z0[1]),
    .z2(Op3_z0[2]), .z3(Op3_z0[3]), .z4(Op3_z0[4]), .z5(Op3_z0[5]), .BAF(Op3_z0[6]), .BAF_2(Op3_z0[7]),
    .INV_OP(Op3_z0[8]));
  XOR XOR (
    .x0(X[0]), .x1(X[1]), .x2(X[2]), .x3(X[3]), .x4(X[4]), .x5(X[5]), .y0(Y[0]), .y1(Y[1]), .y2(Y[2]),
    .y3(Y[3]), .y4(Y[4]), .y5(Y[5]), .ZF(XOR_z0[6]), .z0(XOR_z0[0]), .z1(XOR_z0[1]), .z2(XOR_z0[2]),
    .z3(XOR_z0[3]), .z4(XOR_z0[4]), .z5(XOR_z0[5]), .BAF(XOR_z0[7]), .INV_OP(XOR_z0[8]));
  AND AND (
    .x0(X[0]), .x1(X[1]), .x2(X[2]), .x3(X[3]), .x4(X[4]), .x5(X[5]), .y0(Y[0]), .y1(Y[1]), .y2(Y[2]),
    .y3(Y[3]), .y4(Y[4]), .y5(Y[5]), .ZF(AND_z0[6]), .z0(AND_z0[0]), .z1(AND_z0[1]), .z2(AND_z0[2]),
    .z3(AND_z0[3]), .z4(AND_z0[4]), .z5(AND_z0[5]), .BAF(AND_z0[7]), .INV_OP(AND_z0[8]));
  OR OR (
    .x0(X[0]), .x1(X[1]), .x2(X[2]), .x3(X[3]), .x4(X[4]), .x5(X[5]), .y0(Y[0]), .y1(Y[1]), .y2(Y[2]),
    .y3(Y[3]), .y4(Y[4]), .y5(Y[5]), .ZF(OR_z0[6]), .z0(OR_z0[0]), .z1(OR_z0[1]), .z2(OR_z0[2]),
    .z3(OR_z0[3]), .z4(OR_z0[4]), .z5(OR_z0[5]), .BAF(OR_z0[7]), .INV_OP(OR_z0[8]));
  ALU alu_1 ();  // open: Function, X, Y, Result
  Multiplexer #(.select(5), .width(9), .enable("false")) multiplexer_1 (
    .in0({9{1'b0}}), .in1(VLD_s0), .in2(NEG_z0), .in3(INC_s0), .in4(DEC_s0), .in5(CMPZ_z0), .in6(INV_s0),
    .in7({9{1'b0}}), .in8(SHL_s0), .in9(SHR_z0), .in10(ROL_z0), .in11(ROR_z0), .in12(NOT_z0), .in13(N1_z0),
    .in14(N0_z0), .in15({9{1'b0}}), .in16(ADD_z0), .in17(SUB_z0), .in18(MUL_z0), .in19(DIV_z0),
    .in20({9{1'b0}}), .in21({9{1'b0}}), .in22({9{1'b0}}), .in23({9{1'b0}}), .in24(op1_z0), .in25(op2_z0),
    .in26(Op3_z0), .in27({9{1'b0}}), .in28(XOR_z0), .in29(AND_z0), .in30(OR_z0), .in31({9{1'b0}}),
    .out({INV_OP, BAF, ZF, out_4}), .sel(in_1));
endmodule

module VLD (
  input  a5,
  input  a4,
  input  a3,
  input  a2,
  input  a1,
  input  a0,
  output s5,
  output s4,
  output s3,
  output s2,
  output s1,
  output s0,
  output ZF,
  output BAF,
  output INV_OP
);

  wire not_1_out, not_2_out, not_3_out, not_4_out, not_5_out, not_6_out;

  not not_1 (not_1_out, a5);
  not not_2 (not_2_out, a4);
  not not_3 (not_3_out, a3);
  not not_4 (not_4_out, a2);
  not not_5 (not_5_out, a1);
  not not_6 (not_6_out, a0);
  or or_1 (s0, not_1_out, not_2_out, not_3_out, not_4_out, not_5_out, not_6_out);

  assign BAF = 1'b0;
  assign INV_OP = 1'b1;
  assign s1 = 1'b0;
  assign s2 = 1'b0;
  assign s3 = 1'b0;
  assign s4 = 1'b0;
  assign s5 = 1'b0;
  assign ZF = 1'b0;
endmodule

module NEG (
  input  a5,
  input  a4,
  input  a3,
  input  a2,
  input  a1,
  input  a0,
  output s5,
  output s4,
  output s3,
  output s2,
  output s1,
  output s0,
  output ZF,
  output BAF,
  output INV_OP
);

  wire not_1_out, not_2_out, not_3_out, not_4_out, not_5_out, not_6_out;

  not not_1 (not_1_out, a5);
  not not_2 (not_2_out, a4);
  not not_3 (not_3_out, a3);
  not not_4 (not_4_out, a2);
  not not_5 (not_5_out, a1);
  not not_6 (not_6_out, a0);
  and and_1 (ZF, a5, a4, a3, a2, a1, a0);
  or or_1 (s0, not_1_out, not_2_out, not_3_out, not_4_out, not_5_out, not_6_out);

  assign BAF = 1'b0;
  assign INV_OP = 1'b1;
  assign s1 = 1'b0;
  assign s2 = 1'b0;
  assign s3 = 1'b0;
  assign s4 = 1'b0;
  assign s5 = 1'b0;
endmodule

module INC (
  input  x5,
  input  x4,
  input  x3,
  input  x2,
  input  x1,
  input  x0,
  output s5,
  output s4,
  output s3,
  output s2,
  output s1,
  output s0,
  output ZF,
  output BAF,
  output INV_OP
);

  wire and_2_out, and_3_out, and_4_out, and_5_out, and_6_out, and_7_out, and_8_out, and_9_out, and_10_out,
       and_11_out, and_12_out, and_13_out, and_14_out, and_15_out, and_16_out, and_17_out, and_18_out,
       and_19_out, and_20_out, and_21_out, and_22_out, and_23_out, and_24_out, and_25_out, and_26_out,
       and_27_out, and_28_out, and_29_out, and_30_out, and_31_out, and_32_out, not_1_out, not_2_out,
       not_3_out, not_4_out, not_5_out, not_6_out, not_7_out, not_8_out, not_9_out, not_10_out, not_11_out,
       not_12_out, not_13_out, not_14_out, not_15_out, not_16_out, not_17_out, not_18_out, not_19_out,
       not_20_out, not_21_out, not_22_out, not_23_out, not_24_out, not_25_out, not_26_out, not_27_out,
       not_28_out, not_29_out, not_30_out, not_31_out, not_32_out, not_33_out, not_34_out, not_35_out,
       not_36_out, not_37_out, not_38_out, not_39_out, not_40_out, not_41_out, not_42_out, not_43_out,
       not_44_out, not_45_out;

  not not_1 (not_1_out, x5);
  not not_2 (not_2_out, x4);
  not not_3 (not_3_out, x3);
  not not_4 (not_4_out, x2);
  not not_5 (not_5_out, x1);
  not not_6 (not_6_out, x4);
  not not_7 (not_7_out, x5);
  not not_8 (not_8_out, x0);
  not not_9 (not_9_out, x3);
  not not_10 (not_10_out, x2);
  not not_11 (not_11_out, x1);
  not not_12 (not_12_out, x3);
  not not_13 (not_13_out, x5);
  not not_14 (not_14_out, x0);
  not not_15 (not_15_out, x4);
  not not_16 (not_16_out, x0);
  not not_17 (not_17_out, x2);
  not not_18 (not_18_out, x1);
  not not_19 (not_19_out, x2);
  not not_20 (not_20_out, x5);
  not not_21 (not_21_out, x0);
  not not_22 (not_22_out, x4);
  not not_23 (not_23_out, x0);
  not not_24 (not_24_out, x3);
  not not_25 (not_25_out, x0);
  not not_26 (not_26_out, x1);
  not not_27 (not_27_out, x1);
  not not_28 (not_28_out, x5);
  not not_29 (not_29_out, x0);
  not not_30 (not_30_out, x4);
  not not_31 (not_31_out, x0);
  not not_32 (not_32_out, x3);
  not not_33 (not_33_out, x0);
  not not_34 (not_34_out, x2);
  not not_35 (not_35_out, x0);
  not not_36 (not_36_out, x5);
  not not_37 (not_37_out, x0);
  not not_38 (not_38_out, x4);
  not not_39 (not_39_out, x0);
  not not_40 (not_40_out, x3);
  not not_41 (not_41_out, x0);
  not not_42 (not_42_out, x2);
  not not_43 (not_43_out, x0);
  not not_44 (not_44_out, x1);
  not not_45 (not_45_out, x0);
  and and_1 (BAF, x5, x4, x3, x2, x1, x0);
  and and_2 (and_2_out, not_1_out, x4, x3, x2, x1, x0);
  and and_3 (and_3_out, x5, not_2_out);
  and and_4 (and_4_out, x5, not_3_out);
  and and_5 (and_5_out, x5, not_4_out);
  and and_6 (and_6_out, x5, not_5_out);
  and and_7 (and_7_out, not_6_out, x3, x2, x1, x0);
  and and_8 (and_8_out, not_7_out, x4, not_8_out);
  and and_9 (and_9_out, x4, not_9_out);
  and and_10 (and_10_out, x4, not_10_out);
  and and_11 (and_11_out, x4, not_11_out);
  and and_12 (and_12_out, not_12_out, x2, x1, x0);
  and and_13 (and_13_out, not_13_out, x3, not_14_out);
  and and_14 (and_14_out, not_15_out, x3, not_16_out);
  and and_15 (and_15_out, x3, not_17_out);
  and and_16 (and_16_out, x3, not_18_out);
  and and_17 (and_17_out, not_19_out, x1, x0);
  and and_18 (and_18_out, not_20_out, x2, not_21_out);
  and and_19 (and_19_out, not_22_out, x2, not_23_out);
  and and_20 (and_20_out, not_24_out, x2, not_25_out);
  and and_21 (and_21_out, x2, not_26_out);
  and and_22 (and_22_out, not_27_out, x0);
  and and_23 (and_23_out, not_28_out, x1, not_29_out);
  and and_24 (and_24_out, not_30_out, x1, not_31_out);
  and and_25 (and_25_out, not_32_out, x1, not_33_out);
  and and_26 (and_26_out, not_34_out, x1, not_35_out);
  and and_27 (and_27_out, not_36_out, not_37_out);
  and and_28 (and_28_out, not_38_out, not_39_out);
  and and_29 (and_29_out, not_40_out, not_41_out);
  and and_30 (and_30_out, not_42_out, not_43_out);
  and and_31 (and_31_out, not_44_out, not_45_out);
  and and_32 (and_32_out, x5, x4, x3, x2, x1, x0);
  or or_1 (s5, and_2_out, and_3_out, and_4_out, and_5_out, and_6_out);
  or or_2 (s4, and_7_out, and_8_out, and_9_out, and_10_out, and_11_out);
  or or_3 (s3, and_12_out, and_13_out, and_14_out, and_15_out, and_16_out);
  or or_4 (s2, and_17_out, and_18_out, and_19_out, and_20_out, and_21_out);
  or or_5 (s1, and_22_out, and_23_out, and_24_out, and_25_out, and_26_out);
  or or_6 (s0, and_27_out, and_28_out, and_29_out, and_30_out, and_31_out, and_32_out);

  assign INV_OP = 1'b1;
  assign ZF = 1'b0;
endmodule

module DEC (
  input  x5,
  input  x4,
  input  x3,
  input  x2,
  input  x1,
  input  x0,
  output s5,
  output s4,
  output s3,
  output s2,
  output s1,
  output s0,
  output ZF,
  output BAF,
  output INV_OP
);

  wire and_2_out, and_3_out, and_4_out, and_5_out, and_6_out, and_7_out, and_8_out, and_9_out, and_10_out,
       and_11_out, and_12_out, and_13_out, and_14_out, and_15_out, and_16_out, and_17_out, and_18_out,
       and_19_out, and_20_out, and_21_out, and_22_out, and_23_out, and_24_out, and_25_out, and_26_out,
       not_1_out, not_2_out, not_3_out, not_4_out, not_5_out, not_6_out, not_7_out, not_8_out, not_9_out,
       not_10_out, not_11_out, not_12_out, not_13_out, not_14_out, not_15_out, not_16_out, not_17_out,
       not_18_out, not_19_out, not_20_out, not_21_out, not_22_out, not_23_out, not_24_out, not_25_out;

  not not_1 (not_1_out, x5);
  not not_2 (not_2_out, x4);
  not not_3 (not_3_out, x3);
  not not_4 (not_4_out, x2);
  not not_5 (not_5_out, x1);
  not not_6 (not_6_out, x0);
  not not_7 (not_7_out, x4);
  not not_8 (not_8_out, x3);
  not not_9 (not_9_out, x2);
  not not_10 (not_10_out, x1);
  not not_11 (not_11_out, x0);
  not not_12 (not_12_out, x3);
  not not_13 (not_13_out, x2);
  not not_14 (not_14_out, x1);
  not not_15 (not_15_out, x0);
  not not_16 (not_16_out, x2);
  not not_17 (not_17_out, x1);
  not not_18 (not_18_out, x0);
  not not_19 (not_19_out, x1);
  not not_20 (not_20_out, x0);
  not not_21 (not_21_out, x0);
  not not_22 (not_22_out, x0);
  not not_23 (not_23_out, x0);
  not not_24 (not_24_out, x0);
  not not_25 (not_25_out, x0);
  and and_1 (BAF, x5, x4, x3, x2, x1, x0);
  and and_2 (and_2_out, not_1_out, not_2_out, not_3_out, not_4_out, not_5_out, not_6_out);
  and and_3 (and_3_out, x5, x0);
  and and_4 (and_4_out, x5, x1);
  and and_5 (and_5_out, x5, x2);
  and and_6 (and_6_out, x5, x3);
  and and_7 (and_7_out, x5, x4);
  and and_8 (and_8_out, not_7_out, not_8_out, not_9_out, not_10_out, not_11_out);
  and and_9 (and_9_out, x4, x0);
  and and_10 (and_10_out, x4, x1);
  and and_11 (and_11_out, x4, x2);
  and and_12 (and_12_out, x4, x3);
  and and_13 (and_13_out, not_12_out, not_13_out, not_14_out, not_15_out);
  and and_14 (and_14_out, x3, x0);
  and and_15 (and_15_out, x3, x1);
  and and_16 (and_16_out, x3, x2);
  and and_17 (and_17_out, not_16_out, not_17_out, not_18_out);
  and and_18 (and_18_out, x2, x0);
  and and_19 (and_19_out, x2, x1);
  and and_20 (and_20_out, not_19_out, not_20_out);
  and and_21 (and_21_out, x1, x0);
  and and_22 (and_22_out, x1, not_21_out);
  and and_23 (and_23_out, x2, not_22_out);
  and and_24 (and_24_out, x3, not_23_out);
  and and_25 (and_25_out, x4, not_24_out);
  and and_26 (and_26_out, x5, not_25_out);
  or or_1 (s5, and_2_out, and_3_out, and_4_out, and_5_out, and_6_out, and_7_out);
  or or_2 (s4, and_8_out, and_9_out, and_10_out, and_11_out, and_12_out);
  or or_3 (s3, and_13_out, and_14_out, and_15_out, and_16_out);
  or or_4 (s2, and_17_out, and_18_out, and_19_out);
  or or_5 (s1, and_20_out, and_21_out);
  or or_6 (s0, and_22_out, and_23_out, and_24_out, and_25_out, and_26_out);

  assign INV_OP = 1'b1;
  assign ZF = 1'b0;
endmodule

module CMPZ (
  input  x5,
  input  x4,
  input  x3,
  input  x2,
  input  x1,
  input  x0,
  output z5,
  output z4,
  output z3,
  output z2,
  output z1,
  output z0,
  output ZF,
  output BAF,
  output INV_OP
);

  wire not_1_out, not_2_out, not_3_out, not_4_out, not_5_out, not_6_out;

  not not_1 (not_1_out, x5);
  not not_2 (not_2_out, x4);
  not not_3 (not_3_out, x3);
  not not_4 (not_4_out, x2);
  not not_5 (not_5_out, x1);
  not not_6 (not_6_out, x0);
  and and_1 (ZF, not_1_out, not_2_out, not_3_out, not_4_out, not_5_out, not_6_out);

  assign BAF = 1'b0;
  assign INV_OP = 1'b1;
  assign z0 = 1'b0;
  assign z1 = 1'b0;
  assign z2 = 1'b0;
  assign z3 = 1'b0;
  assign z4 = 1'b0;
  assign z5 = 1'b0;
endmodule

module INV (
  input  x5,
  input  x4,
  input  x3,
  input  x2,
  input  x1,
  input  x0,
  output s5,
  output s4,
  output s3,
  output s2,
  output s1,
  output s0,
  output ZF,
  output BAF,
  output INV_OP
);

  wire and_1_out, and_2_out, and_3_out, and_4_out, and_5_out, and_6_out, and_7_out, and_8_out, and_9_out,
       and_10_out, and_11_out, and_12_out, and_13_out, and_14_out, and_15_out, and_16_out, and_17_out,
       and_18_out, and_19_out, and_20_out, and_21_out, and_22_out, and_23_out, and_24_out, and_25_out,
       and_26_out, and_27_out, and_28_out, and_29_out, and_30_out, and_31_out, and_32_out, and_33_out,
       and_34_out, and_35_out, and_36_out, and_37_out, and_38_out, and_39_out, and_40_out, and_41_out,
       and_42_out, and_43_out, and_44_out, and_45_out, and_46_out, and_47_out, and_48_out, and_49_out,
       and_50_out, and_51_out, and_52_out, and_53_out, and_54_out, and_55_out, and_56_out, and_57_out,
       and_58_out, and_59_out, and_60_out, and_61_out, and_62_out, and_63_out, and_64_out, and_65_out,
       and_66_out, and_67_out, and_68_out, and_69_out, and_70_out, and_71_out, and_72_out, and_73_out,
       and_74_out, and_75_out, and_76_out, and_77_out, and_78_out, and_79_out, and_80_out, and_81_out,
       and_82_out, and_83_out, not_1_out, not_2_out, not_3_out, not_4_out, not_5_out, not_6_out, not_7_out,
       not_8_out, not_9_out, not_10_out, not_11_out, not_12_out, not_13_out, not_14_out, not_15_out,
       not_16_out, not_17_out, not_18_out, not_19_out, not_20_out, not_21_out, not_22_out, not_23_out,
       not_24_out, not_25_out, not_26_out, not_27_out, not_28_out, not_29_out, not_30_out, not_31_out,
       not_32_out, not_33_out, not_34_out, not_35_out, not_36_out, not_37_out, not_38_out, not_39_out,
       not_40_out, not_41_out, not_42_out, not_43_out, not_44_out, not_45_out, not_46_out, not_47_out,
       not_48_out, not_49_out, not_50_out, not_51_out, not_52_out, not_53_out, not_54_out, not_55_out,
       not_56_out, not_57_out, not_58_out, not_59_out, not_60_out, not_61_out, not_62_out, not_63_out,
       not_64_out, not_65_out, not_66_out, not_67_out, not_68_out, not_69_out, not_70_out, not_71_out,
       not_72_out, not_73_out, not_74_out, not_75_out, not_76_out, not_77_out, not_78_out, not_79_out,
       not_80_out, not_81_out, not_82_out, not_83_out, not_84_out, not_85_out, not_86_out, not_87_out,
       not_88_out, not_89_out, not_90_out, not_91_out, not_92_out, not_93_out, not_94_out, not_95_out,
       not_96_out, not_97_out, not_98_out, not_99_out, not_100_out, not_101_out, not_102_out, not_103_out,
       not_104_out, not_105_out, not_106_out, not_107_out, not_108_out, not_109_out, not_110_out,
       not_111_out, not_112_out, not_113_out, not_114_out, not_115_out, not_116_out, not_117_out,
       not_118_out, not_119_out, not_120_out, not_121_out, not_122_out, not_123_out, not_124_out,
       not_125_out, not_126_out, not_127_out, not_128_out, not_129_out, not_130_out, not_131_out,
       not_132_out, not_133_out, not_134_out, not_135_out, not_136_out, not_137_out, not_138_out,
       not_139_out, not_140_out, not_141_out, not_142_out, not_143_out, not_144_out, not_145_out,
       not_146_out, not_147_out, not_148_out, not_149_out, not_150_out, not_151_out, not_152_out,
       not_153_out, not_154_out, not_155_out, not_156_out, not_157_out, not_158_out, not_159_out,
       not_160_out, not_161_out, not_162_out, not_163_out, not_164_out, not_165_out, not_166_out,
       not_167_out, not_168_out, not_169_out, not_170_out, not_171_out, not_172_out, not_173_out,
       not_174_out, not_175_out, not_176_out, not_177_out, not_178_out, not_179_out, not_180_out, not_181_out;

  not not_1 (not_1_out, x5);
  not not_2 (not_2_out, x4);
  not not_3 (not_3_out, x1);
  not not_4 (not_4_out, x5);
  not not_5 (not_5_out, x3);
  not not_6 (not_6_out, x0);
  not not_7 (not_7_out, x5);
  not not_8 (not_8_out, x1);
  not not_9 (not_9_out, x5);
  not not_10 (not_10_out, x4);
  not not_11 (not_11_out, x1);
  not not_12 (not_12_out, x0);
  not not_13 (not_13_out, x3);
  not not_14 (not_14_out, x1);
  not not_15 (not_15_out, x0);
  not not_16 (not_16_out, x3);
  not not_17 (not_17_out, x4);
  not not_18 (not_18_out, x0);
  not not_19 (not_19_out, x2);
  not not_20 (not_20_out, x5);
  not not_21 (not_21_out, x4);
  not not_22 (not_22_out, x2);
  not not_23 (not_23_out, x0);
  not not_24 (not_24_out, x5);
  not not_25 (not_25_out, x2);
  not not_26 (not_26_out, x0);
  not not_27 (not_27_out, x4);
  not not_28 (not_28_out, x2);
  not not_29 (not_29_out, x5);
  not not_30 (not_30_out, x2);
  not not_31 (not_31_out, x1);
  not not_32 (not_32_out, x5);
  not not_33 (not_33_out, x1);
  not not_34 (not_34_out, x3);
  not not_35 (not_35_out, x4);
  not not_36 (not_36_out, x1);
  not not_37 (not_37_out, x0);
  not not_38 (not_38_out, x4);
  not not_39 (not_39_out, x2);
  not not_40 (not_40_out, x0);
  not not_41 (not_41_out, x0);
  not not_42 (not_42_out, x3);
  not not_43 (not_43_out, x1);
  not not_44 (not_44_out, x0);
  not not_45 (not_45_out, x5);
  not not_46 (not_46_out, x4);
  not not_47 (not_47_out, x2);
  not not_48 (not_48_out, x1);
  not not_49 (not_49_out, x0);
  not not_50 (not_50_out, x5);
  not not_51 (not_51_out, x3);
  not not_52 (not_52_out, x2);
  not not_53 (not_53_out, x5);
  not not_54 (not_54_out, x2);
  not not_55 (not_55_out, x1);
  not not_56 (not_56_out, x5);
  not not_57 (not_57_out, x3);
  not not_58 (not_58_out, x0);
  not not_59 (not_59_out, x5);
  not not_60 (not_60_out, x4);
  not not_61 (not_61_out, x3);
  not not_62 (not_62_out, x2);
  not not_63 (not_63_out, x1);
  not not_64 (not_64_out, x4);
  not not_65 (not_65_out, x2);
  not not_66 (not_66_out, x0);
  not not_67 (not_67_out, x2);
  not not_68 (not_68_out, x0);
  not not_69 (not_69_out, x1);
  not not_70 (not_70_out, x4);
  not not_71 (not_71_out, x3);
  not not_72 (not_72_out, x1);
  not not_73 (not_73_out, x4);
  not not_74 (not_74_out, x2);
  not not_75 (not_75_out, x5);
  not not_76 (not_76_out, x3);
  not not_77 (not_77_out, x2);
  not not_78 (not_78_out, x1);
  not not_79 (not_79_out, x0);
  not not_80 (not_80_out, x5);
  not not_81 (not_81_out, x4);
  not not_82 (not_82_out, x3);
  not not_83 (not_83_out, x1);
  not not_84 (not_84_out, x4);
  not not_85 (not_85_out, x3);
  not not_86 (not_86_out, x1);
  not not_87 (not_87_out, x3);
  not not_88 (not_88_out, x4);
  not not_89 (not_89_out, x1);
  not not_90 (not_90_out, x0);
  not not_91 (not_91_out, x2);
  not not_92 (not_92_out, x0);
  not not_93 (not_93_out, x3);
  not not_94 (not_94_out, x2);
  not not_95 (not_95_out, x0);
  not not_96 (not_96_out, x1);
  not not_97 (not_97_out, x5);
  not not_98 (not_98_out, x4);
  not not_99 (not_99_out, x1);
  not not_100 (not_100_out, x5);
  not not_101 (not_101_out, x4);
  not not_102 (not_102_out, x2);
  not not_103 (not_103_out, x5);
  not not_104 (not_104_out, x3);
  not not_105 (not_105_out, x2);
  not not_106 (not_106_out, x5);
  not not_107 (not_107_out, x2);
  not not_108 (not_108_out, x1);
  not not_109 (not_109_out, x5);
  not not_110 (not_110_out, x3);
  not not_111 (not_111_out, x3);
  not not_112 (not_112_out, x1);
  not not_113 (not_113_out, x4);
  not not_114 (not_114_out, x3);
  not not_115 (not_115_out, x1);
  not not_116 (not_116_out, x0);
  not not_117 (not_117_out, x4);
  not not_118 (not_118_out, x2);
  not not_119 (not_119_out, x0);
  not not_120 (not_120_out, x4);
  not not_121 (not_121_out, x3);
  not not_122 (not_122_out, x2);
  not not_123 (not_123_out, x1);
  not not_124 (not_124_out, x5);
  not not_125 (not_125_out, x4);
  not not_126 (not_126_out, x2);
  not not_127 (not_127_out, x5);
  not not_128 (not_128_out, x2);
  not not_129 (not_129_out, x0);
  not not_130 (not_130_out, x5);
  not not_131 (not_131_out, x3);
  not not_132 (not_132_out, x0);
  not not_133 (not_133_out, x5);
  not not_134 (not_134_out, x3);
  not not_135 (not_135_out, x4);
  not not_136 (not_136_out, x3);
  not not_137 (not_137_out, x1);
  not not_138 (not_138_out, x4);
  not not_139 (not_139_out, x0);
  not not_140 (not_140_out, x4);
  not not_141 (not_141_out, x2);
  not not_142 (not_142_out, x0);
  not not_143 (not_143_out, x2);
  not not_144 (not_144_out, x1);
  not not_145 (not_145_out, x5);
  not not_146 (not_146_out, x4);
  not not_147 (not_147_out, x3);
  not not_148 (not_148_out, x2);
  not not_149 (not_149_out, x0);
  not not_150 (not_150_out, x5);
  not not_151 (not_151_out, x3);
  not not_152 (not_152_out, x2);
  not not_153 (not_153_out, x0);
  not not_154 (not_154_out, x4);
  not not_155 (not_155_out, x3);
  not not_156 (not_156_out, x2);
  not not_157 (not_157_out, x5);
  not not_158 (not_158_out, x4);
  not not_159 (not_159_out, x5);
  not not_160 (not_160_out, x4);
  not not_161 (not_161_out, x2);
  not not_162 (not_162_out, x1);
  not not_163 (not_163_out, x5);
  not not_164 (not_164_out, x0);
  not not_165 (not_165_out, x3);
  not not_166 (not_166_out, x1);
  not not_167 (not_167_out, x1);
  not not_168 (not_168_out, x0);
  not not_169 (not_169_out, x5);
  not not_170 (not_170_out, x2);
  not not_171 (not_171_out, x3);
  not not_172 (not_172_out, x2);
  not not_173 (not_173_out, x4);
  not not_174 (not_174_out, x2);
  not not_175 (not_175_out, x0);
  not not_176 (not_176_out, x3);
  not not_177 (not_177_out, x0);
  not not_178 (not_178_out, x4);
  not not_179 (not_179_out, x1);
  not not_180 (not_180_out, x2);
  not not_181 (not_181_out, x1);
  and and_1 (and_1_out, not_1_out, not_2_out, x2, not_3_out, x0);
  and and_2 (and_2_out, not_4_out, x4, not_5_out, x2, not_6_out);
  and and_3 (and_3_out, not_7_out, x4, x3, not_8_out, x0);
  and and_4 (and_4_out, not_9_out, x4, x3, x2, x0);
  and and_5 (and_5_out, x5, not_10_out, x2, not_11_out, not_12_out);
  and and_6 (and_6_out, x5, not_13_out, x2, not_14_out, not_15_out);
  and and_7 (and_7_out, x5, not_16_out, x2, x1, x0);
  and and_8 (and_8_out, x5, not_17_out, x3, x2, x1);
  and and_9 (and_9_out, x5, x3, x2, x1, not_18_out);
  and and_10 (and_10_out, x5, x4, x3, not_19_out, x1, x0);
  and and_11 (and_11_out, not_20_out, not_21_out, not_22_out, x1, not_23_out);
  and and_12 (and_12_out, not_24_out, x3, not_25_out, x1, not_26_out);
  and and_13 (and_13_out, not_27_out, x3, not_28_out, x1, x0);
  and and_14 (and_14_out, not_29_out, x4, not_30_out, not_31_out, x0);
  and and_15 (and_15_out, not_32_out, x4, x3, x2, x0);
  and and_16 (and_16_out, x4, x3, x2, not_33_out, x0);
  and and_17 (and_17_out, x5, not_34_out, x2, x1, x0);
  and and_18 (and_18_out, x5, not_35_out, x3, not_36_out, not_37_out);
  and and_19 (and_19_out, x5, not_38_out, x3, x1, x0);
  and and_20 (and_20_out, x5, x4, not_39_out, x1, not_40_out);
  and and_21 (and_21_out, x5, x4, x3, x1, not_41_out);
  and and_22 (and_22_out, not_42_out, x2, not_43_out, not_44_out);
  and and_23 (and_23_out, not_45_out, not_46_out, x3, not_47_out, not_48_out, not_49_out);
  and and_24 (and_24_out, not_50_out, x4, not_51_out, not_52_out, x0);
  and and_25 (and_25_out, not_53_out, x4, not_54_out, not_55_out, x0);
  and and_26 (and_26_out, not_56_out, x4, not_57_out, x2, not_58_out);
  and and_27 (and_27_out, not_59_out, x4, x2, x1, x0);
  and and_28 (and_28_out, x5, not_60_out, not_61_out, not_62_out, not_63_out, x0);
  and and_29 (and_29_out, x5, not_64_out, x3, x2, x1, x0);
  and and_30 (and_30_out, x5, x4, not_65_out, x1, not_66_out);
  and and_31 (and_31_out, x5, x4, x3, not_67_out, x1);
  and and_32 (and_32_out, x5, x4, x3, x1, not_68_out);
  and and_33 (and_33_out, x5, x4, x3, x2, not_69_out, x0);
  and and_34 (and_34_out, not_70_out, not_71_out, x2, not_72_out, x0);
  and and_35 (and_35_out, not_73_out, x3, not_74_out, x1, x0);
  and and_36 (and_36_out, not_75_out, x4, not_76_out, not_77_out, not_78_out, not_79_out);
  and and_37 (and_37_out, not_80_out, x4, x3, x2, x1, x0);
  and and_38 (and_38_out, x5, not_81_out, not_82_out, not_83_out, x0);
  and and_39 (and_39_out, x5, not_84_out, not_85_out, x2, not_86_out);
  and and_40 (and_40_out, x5, not_87_out, x2, x1, x0);
  and and_41 (and_41_out, x5, not_88_out, x3, not_89_out, not_90_out);
  and and_42 (and_42_out, x5, x3, not_91_out, x1, x0);
  and and_43 (and_43_out, x5, x3, x2, x1, not_92_out);
  and and_44 (and_44_out, x5, x4, not_93_out, not_94_out, x1, not_95_out);
  and and_45 (and_45_out, x5, x4, x3, x2, not_96_out, x0);
  and and_46 (and_46_out, not_97_out, not_98_out, x2, not_99_out, x0);
  and and_47 (and_47_out, not_100_out, not_101_out, x3, not_102_out, x1);
  and and_48 (and_48_out, not_103_out, x4, not_104_out, not_105_out, x0);
  and and_49 (and_49_out, not_106_out, x4, not_107_out, not_108_out, x0);
  and and_50 (and_50_out, not_109_out, x4, not_110_out, x2, x1);
  and and_51 (and_51_out, x4, not_111_out, x2, x1, x0);
  and and_52 (and_52_out, x4, x3, x2, not_112_out, x0);
  and and_53 (and_53_out, x5, not_113_out, not_114_out, not_115_out, not_116_out);
  and and_54 (and_54_out, x5, not_117_out, x3, x1, x0);
  and and_55 (and_55_out, x5, x3, not_118_out, x1, x0);
  and and_56 (and_56_out, x5, x4, x3, x2, x1, not_119_out);
  and and_57 (and_57_out, not_120_out, not_121_out, not_122_out, not_123_out, x0);
  and and_58 (and_58_out, not_124_out, not_125_out, x3, not_126_out, x1);
  and and_59 (and_59_out, not_127_out, x3, not_128_out, x1, not_129_out);
  and and_60 (and_60_out, not_130_out, x4, not_131_out, x2, not_132_out);
  and and_61 (and_61_out, not_133_out, x4, x2, x1, x0);
  and and_62 (and_62_out, x4, not_134_out, x2, x1, x0);
  and and_63 (and_63_out, x5, not_135_out, not_136_out, not_137_out, x0);
  and and_64 (and_64_out, x5, not_138_out, x3, x2, not_139_out);
  and and_65 (and_65_out, x5, not_140_out, x3, x2, x1);
  and and_66 (and_66_out, x5, x4, not_141_out, x1, not_142_out);
  and and_67 (and_67_out, x5, x4, x3, not_143_out, x1);
  and and_68 (and_68_out, x5, x4, x3, x2, not_144_out, x0);
  and and_69 (and_69_out, not_145_out, not_146_out, not_147_out, not_148_out, not_149_out);
  and and_70 (and_70_out, not_150_out, not_151_out, not_152_out, x1, not_153_out);
  and and_71 (and_71_out, not_154_out, not_155_out, not_156_out, x1);
  and and_72 (and_72_out, not_157_out, not_158_out, x2, x1);
  and and_73 (and_73_out, not_159_out, not_160_out, x3, not_161_out, not_162_out, x0);
  and and_74 (and_74_out, not_163_out, x3, x2, not_164_out);
  and and_75 (and_75_out, x4, not_165_out, x2, not_166_out, x0);
  and and_76 (and_76_out, x4, x3, not_167_out, not_168_out);
  and and_77 (and_77_out, not_169_out, x4, x3, not_170_out, x1, x0);
  and and_78 (and_78_out, x5, not_171_out, not_172_out, x0);
  and and_79 (and_79_out, x5, not_173_out, not_174_out, x1, not_175_out);
  and and_80 (and_80_out, x5, not_176_out, x2, x1, not_177_out);
  and and_81 (and_81_out, x5, not_178_out, x3, x2, not_179_out, x0);
  and and_82 (and_82_out, x5, x4, not_180_out, not_181_out);
  and and_83 (and_83_out, x5, x4, x3, x2, x1, x0);
  or or_1 (s4, and_11_out, and_12_out, and_13_out, and_14_out, and_15_out, and_16_out, and_17_out, and_18_out, and_19_out, and_20_out, and_21_out);
  or or_2 (s5, and_1_out, and_2_out, and_3_out, and_4_out, and_5_out, and_6_out, and_7_out, and_8_out, and_9_out, and_10_out);
  or or_3 (s3, and_22_out, and_23_out, and_24_out, and_25_out, and_26_out, and_27_out, and_28_out, and_29_out, and_30_out, and_31_out, and_32_out, and_33_out);
  or or_4 (s2, and_34_out, and_35_out, and_36_out, and_37_out, and_38_out, and_39_out, and_40_out, and_41_out, and_42_out, and_43_out, and_44_out, and_45_out);
  or or_5 (s1, and_46_out, and_47_out, and_48_out, and_49_out, and_50_out, and_51_out, and_52_out, and_53_out, and_54_out, and_55_out, and_56_out);
  or or_6 (s0, and_57_out, and_58_out, and_59_out, and_60_out, and_61_out, and_62_out, and_63_out, and_64_out, and_65_out, and_66_out, and_67_out, and_68_out);
  or or_7 (BAF, and_69_out, and_70_out, and_71_out, and_72_out, and_73_out, and_74_out, and_75_out, and_76_out, and_77_out, and_78_out, and_79_out, and_80_out, and_81_out, and_82_out, and_83_out);

  assign INV_OP = 1'b1;
  assign ZF = 1'b0;
endmodule

module SUB (
  input  x0,
  input  x1,
  input  x2,
  input  x3,
  input  x4,
  input  x5,
  input  y0,
  input  y1,
  input  y2,
  input  y3,
  input  y4,
  input  y5,
  output z0,
  output z1,
  output z2,
  output z3,
  output z4,
  output z5,
  output ZF,
  output BAF,
  output INV_OP
);

  wire comparator_1_eq, comparator_1_gt, comparator_1_lt, comparator_2_eq, comparator_2_gt, comparator_2_lt,
       not_1_out, not_2_out, not_3_out, not_4_out, not_5_out, not_6_out, not_7_out, not_8_out;
  wire [5:0] adder_1_out;
  wire [6:0] subtractor_1_out;
  wire [6:6] adder_1_cout, divider_1_rem;

  Comparator #(.width(6), .mode("unsigned")) comparator_1 (
    .a({x5, x4, x3, x2, x1, x0}), .b({6{1'b1}}), .gt(comparator_1_gt), .eq(comparator_1_eq),
    .lt(comparator_1_lt));
  Comparator #(.width(6), .mode("unsigned")) comparator_2 (
    .a({y5, y4, y3, y2, y1, y0}), .b({6{1'b1}}), .gt(comparator_2_gt), .eq(comparator_2_eq),
    .lt(comparator_2_lt));
  not not_1 (not_1_out, comparator_1_lt);
  not not_2 (not_2_out, comparator_2_lt);
  Adder #(.width(6)) adder_1 (
    .a({x5, x4, x3, x2, x1, x0}), .b({6{1'b1}}), .out(adder_1_out), .cout(adder_1_cout[6]));  // open: cin
  or or_1 (BAF, comparator_1_gt, comparator_1_eq, not_1_out, comparator_2_gt, comparator_2_eq, not_2_out);
  and and_1 (ZF, not_3_out, not_4_out, not_5_out, not_6_out, not_7_out, not_8_out);
  Subtractor #(.width(7)) subtractor_1 (
    .a({adder_1_cout[6], adder_1_out}), .b({1'b0, y5, y4, y3, y2, y1, y0}), .out(subtractor_1_out));  // open: bin, bout
  not not_3 (not_3_out, z0);
  not not_4 (not_4_out, z1);
  not not_5 (not_5_out, z2);
  not not_6 (not_6_out, z3);
  not not_7 (not_7_out, z4);
  not not_8 (not_8_out, z5);
  Divider #(.width(7)) divider_1 (
    .a(subtractor_1_out), .b(7'b0111111), .rem({divider_1_rem[6], z5, z4, z3, z2, z1, z0}));  // open: out, upper

  assign INV_OP = 1'b1;
endmodule

module ADD (
  input  x0,
  input  x1,
  input  x2,
  input  x3,
  input  x4,
  input  x5,
  input  y0,
  input  y1,
  input  y2,
  input  y3,
  input  y4,
  input  y5,
  output z0,
  output z1,
  output z2,
  output z3,
  output z4,
  output z5,
  output ZF,
  output BAF,
  output INV_OP
);

  wire comparator_1_eq, comparator_1_gt, comparator_1_lt, comparator_2_eq, comparator_2_gt, comparator_2_lt,
       not_1_out, not_2_out, not_3_out, not_4_out, not_5_out, not_6_out, not_7_out, not_8_out;
  wire [5:0] adder_1_out;
  wire [6:6] adder_1_cout, divider_1_rem;

  Comparator #(.width(6), .mode("unsigned")) comparator_1 (
    .a({x5, x4, x3, x2, x1, x0}), .b({6{1'b1}}), .gt(comparator_1_gt), .eq(comparator_1_eq),
    .lt(comparator_1_lt));
  Comparator #(.width(6), .mode("unsigned")) comparator_2 (
    .a({y5, y4, y3, y2, y1, y0}), .b({6{1'b1}}), .gt(comparator_2_gt), .eq(comparator_2_eq),
    .lt(comparator_2_lt));
  not not_1 (not_1_out, comparator_1_lt);
  not not_2 (not_2_out, comparator_2_lt);
  Adder #(.width(6)) adder_1 (
    .a({x5, x4, x3, x2, x1, x0}), .b({y5, y4, y3, y2, y1, y0}), .out(adder_1_out), .cout(adder_1_cout[6]));  // open: cin
  and and_1 (ZF, not_3_out, not_4_out, not_5_out, not_6_out, not_7_out, not_8_out);
  or or_1 (BAF, comparator_1_gt, comparator_1_eq, not_1_out, comparator_2_gt, comparator_2_eq, not_2_out);
  not not_3 (not_3_out, z0);
  not not_4 (not_4_out, z1);
  not not_5 (not_5_out, z2);
  not not_6 (not_6_out, z3);
  not not_7 (not_7_out, z4);
  not not_8 (not_8_out, z5);
  Divider #(.width(7)) divider_1 (
    .a({adder_1_cout[6], adder_1_out}), .b(7'b0111111), .rem({divider_1_rem[6], z5, z4, z3, z2, z1, z0}));  // open: out, upper

  assign INV_OP = 1'b1;
endmodule

module MUL (
  input  x0,
  input  x1,
  input  x2,
  input  x3,
  input  x4,
  input  x5,
  input  y0,
  input  y1,
  input  y2,
  input  y3,
  input  y4,
  input  y5,
  output z0,
  output z1,
  output z2,
  output z3,
  output z4,
  output z5,
  output ZF,
  output BAF,
  output INV_OP
);

  wire comparator_1_eq, comparator_1_gt, comparator_1_lt, comparator_2_eq, comparator_2_gt, comparator_2_lt,
       not_1_out, not_2_out, not_3_out, not_4_out, not_5_out, not_6_out, not_7_out, not_8_out;
  wire [5:0] multiplier_1_cout, multiplier_1_out;
  wire [11:6] divider_1_rem;

  Multiplier #(.width(6)) multiplier_1 (
    .a({x5, x4, x3, x2, x1, x0}), .b({y5, y4, y3, y2, y1, y0}), .out(multiplier_1_out),
    .cout(multiplier_1_cout));  // open: cin
  Comparator #(.width(6), .mode("unsigned")) comparator_1 (
    .a({x5, x4, x3, x2, x1, x0}), .b({6{1'b1}}), .gt(comparator_1_gt), .eq(comparator_1_eq),
    .lt(comparator_1_lt));
  not not_1 (not_1_out, comparator_1_lt);
  Comparator #(.width(6), .mode("unsigned")) comparator_2 (
    .a({y5, y4, y3, y2, y1, y0}), .b({6{1'b1}}), .gt(comparator_2_gt), .eq(comparator_2_eq),
    .lt(comparator_2_lt));
  not not_2 (not_2_out, comparator_2_lt);
  not not_3 (not_3_out, z0);
  not not_4 (not_4_out, z1);
  not not_5 (not_5_out, z2);
  and and_1 (ZF, not_3_out, not_4_out, not_5_out, not_6_out, not_7_out, not_8_out);
  not not_6 (not_6_out, z3);
  not not_7 (not_7_out, z4);
  not not_8 (not_8_out, z5);
  or or_1 (BAF, comparator_1_gt, comparator_1_eq, not_1_out, comparator_2_gt, comparator_2_eq, not_2_out);
  Divider #(.width(12)) divider_1 (
    .a({multiplier_1_cout, multiplier_1_out}), .b(12'h3f), .rem({divider_1_rem, z5, z4, z3, z2, z1, z0}));  // open: out, upper

  assign INV_OP = 1'b1;
endmodule

module DIV (
  input  x0,
  input  x1,
  input  x2,
  input  x3,
  input  x4,
  input  x5,
  input  y0,
  input  y1,
  input  y2,
  input  y3,
  input  y4,
  input  y5,
  output z0,
  output z1,
  output z2,
  output z3,
  output z4,
  output z5,
  output ZF,
  output BAF,
  output INV_OP
);

  wire comparator_1_eq, comparator_1_gt, comparator_1_lt, comparator_2_eq, comparator_2_gt, comparator_2_lt,
       inv_1_baf, not_1_out, not_2_out, not_3_out, not_4_out, not_5_out, not_6_out, not_7_out, not_8_out;
  wire [5:0] inv_1_s0, multiplier_1_cout, multiplier_1_out;
  wire [11:6] divider_1_rem;

  INV inv_1 (
    .x5(y5), .x4(y4), .x3(y3), .x2(y2), .x1(y1), .x0(y0), .s5(inv_1_s0[5]), .s4(inv_1_s0[4]),
    .s3(inv_1_s0[3]), .s2(inv_1_s0[2]), .s1(inv_1_s0[1]), .s0(inv_1_s0[0]), .BAF(inv_1_baf));  // open: ZF, INV_OP
  Comparator #(.width(6), .mode("unsigned")) comparator_1 (
    .a({x5, x4, x3, x2, x1, x0}), .b({6{1'b1}}), .gt(comparator_1_gt), .eq(comparator_1_eq),
    .lt(comparator_1_lt));
  not not_1 (not_1_out, comparator_1_lt);
  Comparator #(.width(6), .mode("unsigned")) comparator_2 (
    .a({y5, y4, y3, y2, y1, y0}), .b({6{1'b1}}), .gt(comparator_2_gt), .eq(comparator_2_eq),
    .lt(comparator_2_lt));
  not not_2 (not_2_out, comparator_2_lt);
  Multiplier #(.width(6)) multiplier_1 (
    .a({x5, x4, x3, x2, x1, x0}), .b(inv_1_s0), .out(multiplier_1_out), .cout(multiplier_1_cout));  // open: cin
  and and_1 (ZF, not_3_out, not_4_out, not_5_out, not_6_out, not_7_out, not_8_out);
  or or_1 (BAF, comparator_1_gt, comparator_1_eq, not_1_out, inv_1_baf, comparator_2_gt, comparator_2_eq, not_2_out);
  not not_3 (not_3_out, z0);
  not not_4 (not_4_out, z1);
  not not_5 (not_5_out, z2);
  not not_6 (not_6_out, z3);
  not not_7 (not_7_out, z4);
  not not_8 (not_8_out, z5);
  Divider #(.width(12)) divider_1 (
    .a({multiplier_1_cout, multiplier_1_out}), .b(12'h3f), .rem({divider_1_rem, z5, z4, z3, z2, z1, z0}));  // open: out, upper

  assign INV_OP = 1'b1;
endmodule

module SHL (
  input  x5,
  input  x4,
  input  x3,
  input  x2,
  input  x1,
  input  x0,
  output s5,
  output s4,
  output s3,
  output s2,
  output s1,
  output s0,
  output ZF,
  output BAF,
  output INV_OP
);

  wire not_1_out, not_2_out, not_3_out, not_4_out, not_5_out, not_6_out;

  not not_1 (not_1_out, x5);
  not not_2 (not_2_out, x4);
  not not_3 (not_3_out, x3);
  not not_4 (not_4_out, x2);
  not not_5 (not_5_out, x1);
  not not_6 (not_6_out, x0);
  and and_1 (ZF, not_1_out, not_2_out, not_3_out, not_4_out, not_5_out, not_6_out);

  assign BAF = 1'b0;
  assign INV_OP = 1'b1;
  assign s0 = 1'b0;
  assign s1 = x0;
  assign s2 = x1;
  assign s3 = x2;
  assign s4 = x3;
  assign s5 = x4;
endmodule

module SHR (
  input  x5,
  input  x4,
  input  x3,
  input  x2,
  input  x1,
  input  x0,
  output z5,
  output z4,
  output z3,
  output z2,
  output z1,
  output z0,
  output ZF,
  output BAF,
  output INV_OP
);

  wire not_1_out, not_2_out, not_3_out, not_4_out, not_5_out, not_6_out;

  not not_1 (not_1_out, x5);
  not not_2 (not_2_out, x4);
  not not_3 (not_3_out, x3);
  not not_4 (not_4_out, x2);
  not not_5 (not_5_out, x1);
  not not_6 (not_6_out, x0);
  and and_1 (ZF, not_1_out, not_2_out, not_3_out, not_4_out, not_5_out, not_6_out);

  assign BAF = 1'b0;
  assign INV_OP = 1'b1;
  assign z0 = x1;
  assign z1 = x2;
  assign z2 = x3;
  assign z3 = x4;
  assign z4 = x5;
  assign z5 = 1'b0;
endmodule

module ROL (
  input  x5,
  input  x4,
  input  x3,
  input  x2,
  input  x1,
  input  x0,
  output z5,
  output z4,
  output z3,
  output z2,
  output z1,
  output z0,
  output ZF,
  output BAF,
  output INV_OP
);

  wire not_1_out, not_2_out, not_3_out, not_4_out, not_5_out, not_6_out;

  not not_1 (not_1_out, x5);
  not not_2 (not_2_out, x4);
  not not_3 (not_3_out, x3);
  not not_4 (not_4_out, x2);
  not not_5 (not_5_out, x1);
  not not_6 (not_6_out, x0);
  and and_1 (ZF, not_1_out, not_2_out, not_3_out, not_4_out, not_5_out, not_6_out);

  assign BAF = 1'b0;
  assign INV_OP = 1'b1;
  assign z0 = x5;
  assign z1 = x0;
  assign z2 = x1;
  assign z3 = x2;
  assign z4 = x3;
  assign z5 = x4;
endmodule

module ROR (
  input  x5,
  input  x4,
  input  x3,
  input  x2,
  input  x1,
  input  x0,
  output z5,
  output z4,
  output z3,
  output z2,
  output z1,
  output z0,
  output ZF,
  output BAF,
  output INV_OP
);

  wire not_1_out, not_2_out, not_3_out, not_4_out, not_5_out, not_6_out;

  not not_1 (not_1_out, x5);
  not not_2 (not_2_out, x4);
  not not_3 (not_3_out, x3);
  not not_4 (not_4_out, x2);
  not not_5 (not_5_out, x1);
  not not_6 (not_6_out, x0);
  and and_1 (ZF, not_1_out, not_2_out, not_3_out, not_4_out, not_5_out, not_6_out);

  assign BAF = 1'b0;
  assign INV_OP = 1'b1;
  assign z0 = x1;
  assign z1 = x2;
  assign z2 = x3;
  assign z3 = x4;
  assign z4 = x5;
  assign z5 = x0;
endmodule

module XOR (
  input  x0,
  input  x1,
  input  x2,
  input  x3,
  input  x4,
  input  x5,
  input  y0,
  input  y1,
  input  y2,
  input  y3,
  input  y4,
  input  y5,
  output z0,
  output z1,
  output z2,
  output z3,
  output z4,
  output z5,
  output ZF,
  output BAF,
  output INV_OP
);

  wire not_1_out, not_2_out, not_3_out, not_4_out, not_5_out, not_6_out;

  and and_1 (ZF, not_1_out, not_2_out, not_3_out, not_4_out, not_5_out, not_6_out);
  not not_1 (not_1_out, z0);
  not not_2 (not_2_out, z1);
  not not_3 (not_3_out, z2);
  not not_4 (not_4_out, z3);
  not not_5 (not_5_out, z4);
  not not_6 (not_6_out, z5);
  assign {z5, z4, z3, z2, z1, z0} = {x5, x4, x3, x2, x1, x0} ^ {y5, y4, y3, y2, y1, y0};  // XOR_Gate xor_1, 6 bits wide

  assign BAF = 1'b0;
  assign INV_OP = 1'b1;
endmodule

module AND (
  input  x0,
  input  x1,
  input  x2,
  input  x3,
  input  x4,
  input  x5,
  input  y0,
  input  y1,
  input  y2,
  input  y3,
  input  y4,
  input  y5,
  output z0,
  output z1,
  output z2,
  output z3,
  output z4,
  output z5,
  output ZF,
  output BAF,
  output INV_OP
);

  wire not_1_out, not_2_out, not_3_out, not_4_out, not_5_out, not_6_out;

  not not_1 (not_1_out, z0);
  not not_2 (not_2_out, z1);
  not not_3 (not_3_out, z2);
  and and_1 (ZF, not_1_out, not_2_out, not_3_out, not_4_out, not_5_out, not_6_out);
  not not_4 (not_4_out, z3);
  not not_5 (not_5_out, z4);
  not not_6 (not_6_out, z5);
  assign {z5, z4, z3, z2, z1, z0} = {x5, x4, x3, x2, x1, x0} & {y5, y4, y3, y2, y1, y0};  // AND_Gate and_2, 6 bits wide

  assign BAF = 1'b0;
  assign INV_OP = 1'b1;
endmodule

module OR (
  input  x0,
  input  x1,
  input  x2,
  input  x3,
  input  x4,
  input  x5,
  input  y0,
  input  y1,
  input  y2,
  input  y3,
  input  y4,
  input  y5,
  output z0,
  output z1,
  output z2,
  output z3,
  output z4,
  output z5,
  output ZF,
  output BAF,
  output INV_OP
);

  wire not_1_out, not_2_out, not_3_out, not_4_out, not_5_out, not_6_out;

  not not_1 (not_1_out, z0);
  not not_2 (not_2_out, z1);
  not not_3 (not_3_out, z2);
  and and_1 (ZF, not_1_out, not_2_out, not_3_out, not_4_out, not_5_out, not_6_out);
  not not_4 (not_4_out, z3);
  not not_5 (not_5_out, z4);
  not not_6 (not_6_out, z5);
  assign {z5, z4, z3, z2, z1, z0} = {x5, x4, x3, x2, x1, x0} | {y5, y4, y3, y2, y1, y0};  // OR_Gate or_1, 6 bits wide

  assign BAF = 1'b0;
  assign INV_OP = 1'b1;
endmodule

module NOT (
  input  x0,
  input  x1,
  input  x2,
  input  x3,
  input  x4,
  input  x5,
  output z0,
  output z1,
  output z2,
  output z3,
  output z4,
  output z5,
  output ZF,
  output BAF,
  output INV_OP
);

  wire not_1_out, not_2_out, not_3_out, not_4_out, not_5_out, not_6_out;

  not not_1 (not_1_out, z0);
  not not_2 (not_2_out, z1);
  not not_3 (not_3_out, z2);
  and and_1 (ZF, not_1_out, not_2_out, not_3_out, not_4_out, not_5_out, not_6_out);
  not not_4 (not_4_out, z3);
  not not_5 (not_5_out, z4);
  not not_6 (not_6_out, z5);
  assign {z5, z4, z3, z2, z1, z0} = ~{x5, x4, x3, x2, x1, x0};  // NOT_Gate not_7, 6 bits wide

  assign BAF = 1'b0;
  assign INV_OP = 1'b1;
endmodule

module N1 (
  input  x5,
  input  x4,
  input  x3,
  input  x2,
  input  x1,
  input  x0,
  output z5,
  output z4,
  output z3,
  output z2,
  output z1,
  output z0,
  output ZF,
  output BAF,
  output INV_OP
);

  wire and_1_out, and_2_out, and_3_out, and_4_out, and_5_out, and_6_out, and_7_out, and_8_out, and_9_out,
       and_10_out, and_11_out, and_12_out, and_13_out, and_14_out, and_15_out, and_16_out, and_17_out,
       and_18_out, and_19_out, and_20_out, and_21_out, and_22_out, and_23_out, and_24_out, and_25_out,
       and_26_out, and_27_out, and_28_out, and_29_out, and_30_out, and_31_out, and_32_out, and_33_out,
       and_34_out, and_35_out, and_36_out, and_37_out, and_38_out, and_39_out, and_40_out, and_41_out,
       and_42_out, and_43_out, and_44_out, and_45_out, and_46_out, and_47_out, and_48_out, and_49_out,
       and_50_out, and_51_out, and_52_out, and_53_out, and_54_out, and_55_out, and_56_out, and_57_out,
       and_58_out, and_59_out, and_60_out, and_61_out, and_62_out, and_63_out, and_64_out, and_65_out,
       and_66_out, and_67_out, and_68_out, and_69_out, and_70_out, and_71_out, and_72_out, and_73_out,
       not_1_out, not_2_out, not_3_out, not_4_out, not_5_out, not_6_out, not_7_out, not_8_out, not_9_out,
       not_10_out, not_11_out, not_12_out, not_13_out, not_14_out, not_15_out, not_16_out, not_17_out,
       not_18_out, not_19_out, not_20_out, not_21_out, not_22_out, not_23_out, not_24_out, not_25_out,
       not_26_out, not_27_out, not_28_out, not_29_out, not_30_out, not_31_out, not_32_out, not_33_out,
       not_34_out, not_35_out, not_36_out, not_37_out, not_38_out, not_39_out, not_40_out, not_41_out,
       not_42_out, not_43_out, not_44_out, not_45_out, not_46_out, not_47_out, not_48_out, not_49_out,
       not_50_out, not_51_out, not_52_out, not_53_out, not_54_out, not_55_out, not_56_out, not_57_out,
       not_58_out, not_59_out, not_60_out, not_61_out, not_62_out, not_63_out, not_64_out, not_65_out,
       not_66_out, not_67_out, not_68_out, not_69_out, not_70_out, not_71_out, not_72_out, not_73_out,
       not_74_out, not_75_out, not_76_out, not_77_out, not_78_out, not_79_out, not_80_out, not_81_out,
       not_82_out, not_83_out, not_84_out, not_85_out, not_86_out, not_87_out, not_88_out, not_89_out,
       not_90_out, not_91_out, not_92_out, not_93_out, not_94_out, not_95_out, not_96_out, not_97_out,
       not_98_out, not_99_out, not_100_out, not_101_out, not_102_out, not_103_out, not_104_out, not_105_out,
       not_106_out, not_107_out, not_108_out, not_109_out, not_110_out, not_111_out, not_112_out,
       not_113_out, not_114_out, not_115_out, not_116_out, not_117_out, not_118_out, not_119_out,
       not_120_out, not_121_out, not_122_out, not_123_out, not_124_out, not_125_out, not_126_out,
       not_127_out, not_128_out, not_129_out, not_130_out, not_131_out, not_132_out, not_133_out,
       not_134_out, not_135_out, not_136_out, not_137_out, not_138_out, not_139_out, not_140_out,
       not_141_out, not_142_out, not_143_out, not_144_out, not_145_out, not_146_out, not_147_out,
       not_148_out, not_149_out, not_150_out, not_151_out, not_152_out, not_153_out, not_154_out,
       not_155_out, not_156_out, not_157_out, not_158_out, not_159_out, not_160_out, not_161_out,
       not_162_out, not_163_out, not_164_out, not_165_out, not_166_out, not_167_out, not_168_out,
       not_169_out, not_170_out, not_171_out, not_172_out, not_173_out, not_174_out, not_175_out,
       not_176_out, not_177_out;

  and and_1 (and_1_out, x3, x2, x1, x0);
  and and_2 (and_2_out, x4, x2, x1, x0);
  and and_3 (and_3_out, x4, x3, x1, x0);
  and and_4 (and_4_out, x4, x3, x2, x0);
  and and_5 (and_5_out, x4, x3, x2, x1);
  and and_6 (and_6_out, x5, x2, x1, x0);
  and and_7 (and_7_out, x5, x3, x1, x0);
  and and_8 (and_8_out, x5, x3, x2, x0);
  and and_9 (and_9_out, x5, x3, x2, x1);
  and and_10 (and_10_out, x5, x4, x1, x0);
  and and_11 (and_11_out, x5, x4, x2, x0);
  and and_12 (and_12_out, x5, x4, x2, x1);
  and and_13 (and_13_out, x5, x4, x3, x0);
  and and_14 (and_14_out, x5, x4, x3, x1);
  and and_15 (and_15_out, x5, x4, x3, x2);
  not not_1 (not_1_out, x5);
  not not_2 (not_2_out, x4);
  not not_3 (not_3_out, x3);
  not not_4 (not_4_out, x5);
  not not_5 (not_5_out, x4);
  not not_6 (not_6_out, x3);
  not not_7 (not_7_out, x5);
  not not_8 (not_8_out, x4);
  not not_9 (not_9_out, x3);
  not not_10 (not_10_out, x5);
  not not_11 (not_11_out, x4);
  not not_12 (not_12_out, x2);
  not not_13 (not_13_out, x5);
  not not_14 (not_14_out, x4);
  not not_15 (not_15_out, x2);
  not not_16 (not_16_out, x5);
  not not_17 (not_17_out, x4);
  not not_18 (not_18_out, x1);
  not not_19 (not_19_out, x5);
  not not_20 (not_20_out, x4);
  not not_21 (not_21_out, x0);
  not not_22 (not_22_out, x5);
  not not_23 (not_23_out, x3);
  not not_24 (not_24_out, x2);
  not not_25 (not_25_out, x5);
  not not_26 (not_26_out, x3);
  not not_27 (not_27_out, x2);
  not not_28 (not_28_out, x5);
  not not_29 (not_29_out, x3);
  not not_30 (not_30_out, x1);
  not not_31 (not_31_out, x5);
  not not_32 (not_32_out, x3);
  not not_33 (not_33_out, x0);
  not not_34 (not_34_out, x5);
  not not_35 (not_35_out, x2);
  not not_36 (not_36_out, x1);
  not not_37 (not_37_out, x5);
  not not_38 (not_38_out, x2);
  not not_39 (not_39_out, x0);
  not not_40 (not_40_out, x5);
  not not_41 (not_41_out, x1);
  not not_42 (not_42_out, x0);
  not not_43 (not_43_out, x4);
  not not_44 (not_44_out, x3);
  not not_45 (not_45_out, x2);
  not not_46 (not_46_out, x4);
  not not_47 (not_47_out, x3);
  not not_48 (not_48_out, x2);
  not not_49 (not_49_out, x4);
  not not_50 (not_50_out, x3);
  not not_51 (not_51_out, x1);
  not not_52 (not_52_out, x4);
  not not_53 (not_53_out, x3);
  not not_54 (not_54_out, x0);
  not not_55 (not_55_out, x4);
  not not_56 (not_56_out, x2);
  not not_57 (not_57_out, x1);
  not not_58 (not_58_out, x4);
  not not_59 (not_59_out, x2);
  not not_60 (not_60_out, x0);
  not not_61 (not_61_out, x4);
  not not_62 (not_62_out, x1);
  not not_63 (not_63_out, x0);
  not not_64 (not_64_out, x3);
  not not_65 (not_65_out, x2);
  not not_66 (not_66_out, x1);
  not not_67 (not_67_out, x3);
  not not_68 (not_68_out, x2);
  not not_69 (not_69_out, x0);
  not not_70 (not_70_out, x3);
  not not_71 (not_71_out, x1);
  not not_72 (not_72_out, x0);
  not not_73 (not_73_out, x2);
  not not_74 (not_74_out, x1);
  not not_75 (not_75_out, x0);
  not not_76 (not_76_out, x5);
  not not_77 (not_77_out, x4);
  not not_78 (not_78_out, x3);
  not not_79 (not_79_out, x2);
  not not_80 (not_80_out, x1);
  not not_81 (not_81_out, x5);
  not not_82 (not_82_out, x4);
  not not_83 (not_83_out, x3);
  not not_84 (not_84_out, x2);
  not not_85 (not_85_out, x0);
  not not_86 (not_86_out, x5);
  not not_87 (not_87_out, x4);
  not not_88 (not_88_out, x3);
  not not_89 (not_89_out, x1);
  not not_90 (not_90_out, x0);
  not not_91 (not_91_out, x5);
  not not_92 (not_92_out, x4);
  not not_93 (not_93_out, x3);
  not not_94 (not_94_out, x5);
  not not_95 (not_95_out, x4);
  not not_96 (not_96_out, x2);
  not not_97 (not_97_out, x1);
  not not_98 (not_98_out, x0);
  not not_99 (not_99_out, x5);
  not not_100 (not_100_out, x4);
  not not_101 (not_101_out, x2);
  not not_102 (not_102_out, x5);
  not not_103 (not_103_out, x4);
  not not_104 (not_104_out, x1);
  not not_105 (not_105_out, x5);
  not not_106 (not_106_out, x4);
  not not_107 (not_107_out, x0);
  not not_108 (not_108_out, x5);
  not not_109 (not_109_out, x3);
  not not_110 (not_110_out, x2);
  not not_111 (not_111_out, x1);
  not not_112 (not_112_out, x0);
  not not_113 (not_113_out, x5);
  not not_114 (not_114_out, x3);
  not not_115 (not_115_out, x2);
  not not_116 (not_116_out, x5);
  not not_117 (not_117_out, x3);
  not not_118 (not_118_out, x1);
  not not_119 (not_119_out, x5);
  not not_120 (not_120_out, x3);
  not not_121 (not_121_out, x0);
  not not_122 (not_122_out, x5);
  not not_123 (not_123_out, x2);
  not not_124 (not_124_out, x1);
  not not_125 (not_125_out, x5);
  not not_126 (not_126_out, x2);
  not not_127 (not_127_out, x0);
  not not_128 (not_128_out, x5);
  not not_129 (not_129_out, x1);
  not not_130 (not_130_out, x0);
  not not_131 (not_131_out, x5);
  not not_132 (not_132_out, x4);
  not not_133 (not_133_out, x3);
  not not_134 (not_134_out, x2);
  not not_135 (not_135_out, x1);
  not not_136 (not_136_out, x0);
  not not_137 (not_137_out, x4);
  not not_138 (not_138_out, x3);
  not not_139 (not_139_out, x2);
  not not_140 (not_140_out, x4);
  not not_141 (not_141_out, x3);
  not not_142 (not_142_out, x1);
  not not_143 (not_143_out, x4);
  not not_144 (not_144_out, x3);
  not not_145 (not_145_out, x0);
  not not_146 (not_146_out, x4);
  not not_147 (not_147_out, x2);
  not not_148 (not_148_out, x1);
  not not_149 (not_149_out, x4);
  not not_150 (not_150_out, x2);
  not not_151 (not_151_out, x0);
  not not_152 (not_152_out, x4);
  not not_153 (not_153_out, x1);
  not not_154 (not_154_out, x0);
  not not_155 (not_155_out, x4);
  not not_156 (not_156_out, x3);
  not not_157 (not_157_out, x2);
  not not_158 (not_158_out, x1);
  not not_159 (not_159_out, x3);
  not not_160 (not_160_out, x2);
  not not_161 (not_161_out, x0);
  not not_162 (not_162_out, x3);
  not not_163 (not_163_out, x1);
  not not_164 (not_164_out, x0);
  not not_165 (not_165_out, x3);
  not not_166 (not_166_out, x2);
  not not_167 (not_167_out, x1);
  not not_168 (not_168_out, x0);
  not not_169 (not_169_out, x2);
  not not_170 (not_170_out, x1);
  not not_171 (not_171_out, x0);
  not not_172 (not_172_out, x5);
  not not_173 (not_173_out, x4);
  not not_174 (not_174_out, x3);
  not not_175 (not_175_out, x2);
  not not_176 (not_176_out, x1);
  not not_177 (not_177_out, x0);
  and and_16 (and_16_out, not_1_out, not_2_out, not_3_out, x1, x0);
  and and_17 (and_17_out, not_4_out, not_5_out, not_6_out, x2, x0);
  and and_18 (and_18_out, not_7_out, not_8_out, not_9_out, x2, x1);
  and and_19 (and_19_out, not_10_out, not_11_out, x3, not_12_out, x0);
  and and_20 (and_20_out, not_13_out, not_14_out, x3, not_15_out, x1);
  and and_21 (and_21_out, not_16_out, not_17_out, x3, x2, not_18_out);
  and and_22 (and_22_out, not_19_out, not_20_out, x3, x2, not_21_out);
  and and_23 (and_23_out, not_22_out, x4, not_23_out, not_24_out, x0);
  and and_24 (and_24_out, not_25_out, x4, not_26_out, not_27_out, x1);
  and and_25 (and_25_out, not_28_out, x4, not_29_out, x2, not_30_out);
  and and_26 (and_26_out, not_31_out, x4, not_32_out, x2, not_33_out);
  and and_27 (and_27_out, not_34_out, x4, x3, not_35_out, not_36_out);
  and and_28 (and_28_out, not_37_out, x4, x3, not_38_out, not_39_out);
  and and_29 (and_29_out, not_40_out, x4, x3, not_41_out, not_42_out);
  and and_30 (and_30_out, x5, not_43_out, not_44_out, not_45_out, x0);
  and and_31 (and_31_out, x5, not_46_out, not_47_out, not_48_out, x1);
  and and_32 (and_32_out, x5, not_49_out, not_50_out, x2, not_51_out);
  and and_33 (and_33_out, x5, not_52_out, not_53_out, x2, not_54_out);
  and and_34 (and_34_out, x5, not_55_out, x3, not_56_out, not_57_out);
  and and_35 (and_35_out, x5, not_58_out, x3, not_59_out, not_60_out);
  and and_36 (and_36_out, x5, not_61_out, x3, not_62_out, not_63_out);
  and and_37 (and_37_out, x5, x4, not_64_out, not_65_out, not_66_out);
  and and_38 (and_38_out, x5, x4, not_67_out, not_68_out, not_69_out);
  and and_39 (and_39_out, x5, x4, not_70_out, not_71_out, not_72_out);
  and and_40 (and_40_out, x5, x4, not_73_out, not_74_out, not_75_out);
  and and_41 (and_41_out, x5, x4, x3, x2, x1, x0);
  and and_42 (and_42_out, not_76_out, not_77_out, not_78_out, not_79_out, not_80_out, x0);
  and and_43 (and_43_out, not_81_out, not_82_out, not_83_out, not_84_out, x1, not_85_out);
  and and_44 (and_44_out, not_86_out, not_87_out, not_88_out, x2, not_89_out, not_90_out);
  and and_45 (and_45_out, not_91_out, not_92_out, not_93_out, x2, x1, x0);
  and and_46 (and_46_out, not_94_out, not_95_out, x3, not_96_out, not_97_out, not_98_out);
  and and_47 (and_47_out, not_99_out, not_100_out, x3, not_101_out, x1, x0);
  and and_48 (and_48_out, not_102_out, not_103_out, x3, x2, not_104_out, x0);
  and and_49 (and_49_out, not_105_out, not_106_out, x3, x2, x1, not_107_out);
  and and_50 (and_50_out, not_108_out, x4, not_109_out, not_110_out, not_111_out, not_112_out);
  and and_51 (and_51_out, not_113_out, x4, not_114_out, not_115_out, x1, x0);
  and and_52 (and_52_out, not_116_out, x4, not_117_out, x2, not_118_out, x0);
  and and_53 (and_53_out, not_119_out, x4, not_120_out, x2, x1, not_121_out);
  and and_54 (and_54_out, not_122_out, x4, x3, not_123_out, not_124_out, x0);
  and and_55 (and_55_out, not_125_out, x4, x3, not_126_out, x1, not_127_out);
  and and_56 (and_56_out, not_128_out, x4, x3, x2, not_129_out, not_130_out);
  and and_57 (and_57_out, not_131_out, x4, x3, x2, x1, x0);
  and and_58 (and_58_out, x5, not_132_out, not_133_out, not_134_out, not_135_out, not_136_out);
  and and_59 (and_59_out, x5, not_137_out, not_138_out, not_139_out, x1, x0);
  and and_60 (and_60_out, x5, not_140_out, not_141_out, x2, not_142_out, x0);
  and and_61 (and_61_out, x5, not_143_out, not_144_out, x2, x1, not_145_out);
  and and_62 (and_62_out, x5, not_146_out, x3, not_147_out, not_148_out, x0);
  and and_63 (and_63_out, x5, not_149_out, x3, not_150_out, x1, not_151_out);
  and and_64 (and_64_out, x5, not_152_out, x3, x2, not_153_out, not_154_out);
  and and_65 (and_65_out, x5, not_155_out, x3, x2, x1, x0);
  and and_66 (and_66_out, x5, x4, not_156_out, not_157_out, not_158_out, x0);
  and and_67 (and_67_out, x5, x4, not_159_out, not_160_out, x1, not_161_out);
  and and_68 (and_68_out, x5, x4, not_162_out, x2, not_163_out, not_164_out);
  and and_69 (and_69_out, x5, x4, not_165_out, x2, x1, x0);
  and and_70 (and_70_out, x5, x4, x3, not_166_out, not_167_out, not_168_out);
  and and_71 (and_71_out, x5, x4, x3, not_169_out, x1, x0);
  and and_72 (and_72_out, x5, x4, x3, x2, not_170_out, x0);
  and and_73 (and_73_out, x5, x4, x3, x2, x1, not_171_out);
  and and_74 (ZF, not_172_out, not_173_out, not_174_out, not_175_out, not_176_out, not_177_out);
  or or_1 (z2, and_1_out, and_2_out, and_3_out, and_4_out, and_5_out, and_6_out, and_7_out, and_8_out, and_9_out, and_10_out, and_11_out, and_12_out, and_13_out, and_14_out, and_15_out);
  or or_2 (z1, and_16_out, and_17_out, and_18_out, and_19_out, and_20_out, and_21_out, and_22_out, and_23_out, and_24_out, and_25_out, and_26_out, and_27_out, and_28_out, and_29_out, and_30_out, and_31_out, and_32_out, and_33_out, and_34_out, and_35_out, and_36_out, and_37_out, and_38_out, and_39_out, and_40_out, and_41_out);
  or or_3 (z0, and_42_out, and_43_out, and_44_out, and_45_out, and_46_out, and_47_out, and_48_out, and_49_out, and_50_out, and_51_out, and_52_out, and_53_out, and_54_out, and_55_out, and_56_out, and_57_out, and_58_out, and_59_out, and_60_out, and_61_out, and_62_out, and_63_out, and_64_out, and_65_out, and_66_out, and_67_out, and_68_out, and_69_out, and_70_out, and_71_out, and_72_out, and_73_out);

  assign BAF = 1'b0;
  assign INV_OP = 1'b1;
  assign z3 = 1'b0;
  assign z4 = 1'b0;
  assign z5 = 1'b0;
endmodule

module N0 (
  input  x5,
  input  x4,
  input  x3,
  input  x2,
  input  x1,
  input  x0,
  output z5,
  output z4,
  output z3,
  output z2,
  output z1,
  output z0,
  output ZF,
  output BAF,
  output INV_OP
);

  wire and_2_out, and_3_out, and_4_out, and_5_out, and_6_out, and_7_out, and_8_out, and_9_out, and_10_out,
       and_11_out, and_12_out, and_13_out, and_14_out, and_15_out, and_16_out, and_17_out, and_18_out,
       and_19_out, and_20_out, and_21_out, and_22_out, and_23_out, and_24_out, and_25_out, and_26_out,
       and_27_out, and_28_out, and_29_out, and_30_out, and_31_out, and_32_out, and_33_out, and_34_out,
       and_35_out, and_36_out, and_37_out, and_38_out, and_39_out, and_40_out, and_41_out, and_42_out,
       and_43_out, and_44_out, and_45_out, and_46_out, and_47_out, and_48_out, and_49_out, and_50_out,
       and_51_out, and_52_out, and_53_out, and_54_out, and_55_out, and_56_out, and_57_out, and_58_out,
       and_59_out, and_60_out, and_61_out, and_62_out, and_63_out, and_64_out, and_65_out, and_66_out,
       and_67_out, and_68_out, and_69_out, and_70_out, and_71_out, and_72_out, and_73_out, and_74_out,
       not_1_out, not_2_out, not_3_out, not_4_out, not_5_out, not_6_out, not_7_out, not_8_out, not_9_out,
       not_10_out, not_11_out, not_12_out, not_13_out, not_14_out, not_15_out, not_16_out, not_17_out,
       not_18_out, not_19_out, not_20_out, not_21_out, not_22_out, not_23_out, not_24_out, not_25_out,
       not_26_out, not_27_out, not_28_out, not_29_out, not_30_out, not_31_out, not_32_out, not_33_out,
       not_34_out, not_35_out, not_36_out, not_37_out, not_38_out, not_39_out, not_40_out, not_41_out,
       not_42_out, not_43_out, not_44_out, not_45_out, not_46_out, not_47_out, not_48_out, not_49_out,
       not_50_out, not_51_out, not_52_out, not_53_out, not_54_out, not_55_out, not_56_out, not_57_out,
       not_58_out, not_59_out, not_60_out, not_61_out, not_62_out, not_63_out, not_64_out, not_65_out,
       not_66_out, not_67_out, not_68_out, not_69_out, not_70_out, not_71_out, not_72_out, not_73_out,
       not_74_out, not_75_out, not_76_out, not_77_out, not_78_out, not_79_out, not_80_out, not_81_out,
       not_82_out, not_83_out, not_84_out, not_85_out, not_86_out, not_87_out, not_88_out, not_89_out,
       not_90_out, not_91_out, not_92_out, not_93_out, not_94_out, not_95_out, not_96_out, not_97_out,
       not_98_out, not_99_out, not_100_out, not_101_out, not_102_out, not_103_out, not_104_out, not_105_out,
       not_106_out, not_107_out, not_108_out, not_109_out, not_110_out, not_111_out, not_112_out,
       not_113_out, not_114_out, not_115_out, not_116_out, not_117_out, not_118_out, not_119_out,
       not_120_out, not_121_out, not_122_out, not_123_out, not_124_out, not_125_out, not_126_out,
       not_127_out, not_128_out, not_129_out, not_130_out, not_131_out, not_132_out, not_133_out,
       not_134_out, not_135_out, not_136_out, not_137_out, not_138_out, not_139_out, not_140_out,
       not_141_out, not_142_out, not_143_out, not_144_out, not_145_out, not_146_out, not_147_out,
       not_148_out, not_149_out, not_150_out, not_151_out, not_152_out, not_153_out, not_154_out,
       not_155_out, not_156_out, not_157_out, not_158_out, not_159_out, not_160_out, not_161_out,
       not_162_out, not_163_out, not_164_out, not_165_out, not_166_out, not_167_out, not_168_out,
       not_169_out, not_170_out, not_171_out, not_172_out, not_173_out, not_174_out, not_175_out,
       not_176_out, not_177_out, not_178_out, not_179_out, not_180_out, not_181_out, not_182_out,
       not_183_out, not_184_out, not_185_out, not_186_out, not_187_out, not_188_out, not_189_out,
       not_190_out, not_191_out, not_192_out, not_193_out, not_194_out, not_195_out, not_196_out,
       not_197_out, not_198_out, not_199_out, not_200_out, not_201_out, not_202_out, not_203_out,
       not_204_out, not_205_out, not_206_out, not_207_out, not_208_out, not_209_out, not_210_out,
       not_211_out, not_212_out;

  not not_1 (not_1_out, x5);
  not not_2 (not_2_out, x4);
  not not_3 (not_3_out, x3);
  not not_4 (not_4_out, x2);
  not not_5 (not_5_out, x5);
  not not_6 (not_6_out, x4);
  not not_7 (not_7_out, x3);
  not not_8 (not_8_out, x1);
  not not_9 (not_9_out, x5);
  not not_10 (not_10_out, x4);
  not not_11 (not_11_out, x3);
  not not_12 (not_12_out, x0);
  not not_13 (not_13_out, x5);
  not not_14 (not_14_out, x4);
  not not_15 (not_15_out, x2);
  not not_16 (not_16_out, x1);
  not not_17 (not_17_out, x5);
  not not_18 (not_18_out, x4);
  not not_19 (not_19_out, x2);
  not not_20 (not_20_out, x0);
  not not_21 (not_21_out, x5);
  not not_22 (not_22_out, x4);
  not not_23 (not_23_out, x1);
  not not_24 (not_24_out, x0);
  not not_25 (not_25_out, x5);
  not not_26 (not_26_out, x3);
  not not_27 (not_27_out, x2);
  not not_28 (not_28_out, x1);
  not not_29 (not_29_out, x5);
  not not_30 (not_30_out, x3);
  not not_31 (not_31_out, x2);
  not not_32 (not_32_out, x0);
  not not_33 (not_33_out, x5);
  not not_34 (not_34_out, x3);
  not not_35 (not_35_out, x1);
  not not_36 (not_36_out, x0);
  not not_37 (not_37_out, x5);
  not not_38 (not_38_out, x2);
  not not_39 (not_39_out, x1);
  not not_40 (not_40_out, x0);
  not not_41 (not_41_out, x4);
  not not_42 (not_42_out, x3);
  not not_43 (not_43_out, x2);
  not not_44 (not_44_out, x1);
  not not_45 (not_45_out, x4);
  not not_46 (not_46_out, x3);
  not not_47 (not_47_out, x2);
  not not_48 (not_48_out, x0);
  not not_49 (not_49_out, x4);
  not not_50 (not_50_out, x3);
  not not_51 (not_51_out, x1);
  not not_52 (not_52_out, x0);
  not not_53 (not_53_out, x4);
  not not_54 (not_54_out, x2);
  not not_55 (not_55_out, x1);
  not not_56 (not_56_out, x0);
  not not_57 (not_57_out, x3);
  not not_58 (not_58_out, x2);
  not not_59 (not_59_out, x1);
  not not_60 (not_60_out, x0);
  not not_61 (not_61_out, x5);
  not not_62 (not_62_out, x4);
  not not_63 (not_63_out, x3);
  not not_64 (not_64_out, x2);
  not not_65 (not_65_out, x1);
  not not_66 (not_66_out, x0);
  not not_67 (not_67_out, x5);
  not not_68 (not_68_out, x4);
  not not_69 (not_69_out, x5);
  not not_70 (not_70_out, x4);
  not not_71 (not_71_out, x5);
  not not_72 (not_72_out, x4);
  not not_73 (not_73_out, x5);
  not not_74 (not_74_out, x4);
  not not_75 (not_75_out, x5);
  not not_76 (not_76_out, x3);
  not not_77 (not_77_out, x5);
  not not_78 (not_78_out, x3);
  not not_79 (not_79_out, x5);
  not not_80 (not_80_out, x3);
  not not_81 (not_81_out, x5);
  not not_82 (not_82_out, x2);
  not not_83 (not_83_out, x5);
  not not_84 (not_84_out, x2);
  not not_85 (not_85_out, x5);
  not not_86 (not_86_out, x1);
  not not_87 (not_87_out, x5);
  not not_88 (not_88_out, x0);
  not not_89 (not_89_out, x4);
  not not_90 (not_90_out, x3);
  not not_91 (not_91_out, x4);
  not not_92 (not_92_out, x3);
  not not_93 (not_93_out, x4);
  not not_94 (not_94_out, x3);
  not not_95 (not_95_out, x4);
  not not_96 (not_96_out, x2);
  not not_97 (not_97_out, x4);
  not not_98 (not_98_out, x2);
  not not_99 (not_99_out, x4);
  not not_100 (not_100_out, x1);
  not not_101 (not_101_out, x4);
  not not_102 (not_102_out, x0);
  not not_103 (not_103_out, x3);
  not not_104 (not_104_out, x2);
  not not_105 (not_105_out, x3);
  not not_106 (not_106_out, x2);
  not not_107 (not_107_out, x3);
  not not_108 (not_108_out, x1);
  not not_109 (not_109_out, x3);
  not not_110 (not_110_out, x0);
  not not_111 (not_111_out, x2);
  not not_112 (not_112_out, x1);
  not not_113 (not_113_out, x2);
  not not_114 (not_114_out, x0);
  not not_115 (not_115_out, x1);
  not not_116 (not_116_out, x0);
  not not_117 (not_117_out, x5);
  not not_118 (not_118_out, x4);
  not not_119 (not_119_out, x3);
  not not_120 (not_120_out, x2);
  not not_121 (not_121_out, x1);
  not not_122 (not_122_out, x5);
  not not_123 (not_123_out, x4);
  not not_124 (not_124_out, x3);
  not not_125 (not_125_out, x2);
  not not_126 (not_126_out, x0);
  not not_127 (not_127_out, x5);
  not not_128 (not_128_out, x4);
  not not_129 (not_129_out, x3);
  not not_130 (not_130_out, x1);
  not not_131 (not_131_out, x0);
  not not_132 (not_132_out, x5);
  not not_133 (not_133_out, x4);
  not not_134 (not_134_out, x3);
  not not_135 (not_135_out, x5);
  not not_136 (not_136_out, x4);
  not not_137 (not_137_out, x2);
  not not_138 (not_138_out, x1);
  not not_139 (not_139_out, x0);
  not not_140 (not_140_out, x5);
  not not_141 (not_141_out, x4);
  not not_142 (not_142_out, x2);
  not not_143 (not_143_out, x5);
  not not_144 (not_144_out, x4);
  not not_145 (not_145_out, x1);
  not not_146 (not_146_out, x5);
  not not_147 (not_147_out, x4);
  not not_148 (not_148_out, x0);
  not not_149 (not_149_out, x5);
  not not_150 (not_150_out, x3);
  not not_151 (not_151_out, x2);
  not not_152 (not_152_out, x1);
  not not_153 (not_153_out, x0);
  not not_154 (not_154_out, x5);
  not not_155 (not_155_out, x3);
  not not_156 (not_156_out, x2);
  not not_157 (not_157_out, x5);
  not not_158 (not_158_out, x3);
  not not_159 (not_159_out, x1);
  not not_160 (not_160_out, x5);
  not not_161 (not_161_out, x3);
  not not_162 (not_162_out, x0);
  not not_163 (not_163_out, x5);
  not not_164 (not_164_out, x2);
  not not_165 (not_165_out, x1);
  not not_166 (not_166_out, x5);
  not not_167 (not_167_out, x2);
  not not_168 (not_168_out, x0);
  not not_169 (not_169_out, x5);
  not not_170 (not_170_out, x1);
  not not_171 (not_171_out, x0);
  not not_172 (not_172_out, x5);
  not not_173 (not_173_out, x4);
  not not_174 (not_174_out, x3);
  not not_175 (not_175_out, x2);
  not not_176 (not_176_out, x1);
  not not_177 (not_177_out, x0);
  not not_178 (not_178_out, x4);
  not not_179 (not_179_out, x3);
  not not_180 (not_180_out, x2);
  not not_181 (not_181_out, x4);
  not not_182 (not_182_out, x3);
  not not_183 (not_183_out, x1);
  not not_184 (not_184_out, x4);
  not not_185 (not_185_out, x3);
  not not_186 (not_186_out, x0);
  not not_187 (not_187_out, x4);
  not not_188 (not_188_out, x2);
  not not_189 (not_189_out, x1);
  not not_190 (not_190_out, x4);
  not not_191 (not_191_out, x2);
  not not_192 (not_192_out, x0);
  not not_193 (not_193_out, x4);
  not not_194 (not_194_out, x1);
  not not_195 (not_195_out, x0);
  not not_196 (not_196_out, x4);
  not not_197 (not_197_out, x3);
  not not_198 (not_198_out, x2);
  not not_199 (not_199_out, x1);
  not not_200 (not_200_out, x3);
  not not_201 (not_201_out, x2);
  not not_202 (not_202_out, x0);
  not not_203 (not_203_out, x3);
  not not_204 (not_204_out, x1);
  not not_205 (not_205_out, x0);
  not not_206 (not_206_out, x3);
  not not_207 (not_207_out, x2);
  not not_208 (not_208_out, x1);
  not not_209 (not_209_out, x0);
  not not_210 (not_210_out, x2);
  not not_211 (not_211_out, x1);
  not not_212 (not_212_out, x0);
  and and_1 (ZF, x5, x4, x3, x2, x1, x0);
  and and_2 (and_2_out, not_1_out, not_2_out, not_3_out, not_4_out);
  and and_3 (and_3_out, not_5_out, not_6_out, not_7_out, not_8_out);
  and and_4 (and_4_out, not_9_out, not_10_out, not_11_out, not_12_out);
  and and_5 (and_5_out, not_13_out, not_14_out, not_15_out, not_16_out);
  and and_6 (and_6_out, not_17_out, not_18_out, not_19_out, not_20_out);
  and and_7 (and_7_out, not_21_out, not_22_out, not_23_out, not_24_out);
  and and_8 (and_8_out, not_25_out, not_26_out, not_27_out, not_28_out);
  and and_9 (and_9_out, not_29_out, not_30_out, not_31_out, not_32_out);
  and and_10 (and_10_out, not_33_out, not_34_out, not_35_out, not_36_out);
  and and_11 (and_11_out, not_37_out, not_38_out, not_39_out, not_40_out);
  and and_12 (and_12_out, not_41_out, not_42_out, not_43_out, not_44_out);
  and and_13 (and_13_out, not_45_out, not_46_out, not_47_out, not_48_out);
  and and_14 (and_14_out, not_49_out, not_50_out, not_51_out, not_52_out);
  and and_15 (and_15_out, not_53_out, not_54_out, not_55_out, not_56_out);
  and and_16 (and_16_out, not_57_out, not_58_out, not_59_out, not_60_out);
  and and_17 (and_17_out, not_61_out, not_62_out, not_63_out, not_64_out, not_65_out, not_66_out);
  and and_18 (and_18_out, not_67_out, not_68_out, x2, x1, x0);
  and and_19 (and_19_out, not_69_out, not_70_out, x3, x1, x0);
  and and_20 (and_20_out, not_71_out, not_72_out, x3, x2, x0);
  and and_21 (and_21_out, not_73_out, not_74_out, x3, x2, x1);
  and and_22 (and_22_out, not_75_out, x4, not_76_out, x1, x0);
  and and_23 (and_23_out, not_77_out, x4, not_78_out, x2, x0);
  and and_24 (and_24_out, not_79_out, x4, not_80_out, x2, x1);
  and and_25 (and_25_out, not_81_out, x4, x3, not_82_out, x0);
  and and_26 (and_26_out, not_83_out, x4, x3, not_84_out, x1);
  and and_27 (and_27_out, not_85_out, x4, x3, x2, not_86_out);
  and and_28 (and_28_out, not_87_out, x4, x3, x2, not_88_out);
  and and_29 (and_29_out, x5, not_89_out, not_90_out, x1, x0);
  and and_30 (and_30_out, x5, not_91_out, not_92_out, x2, x0);
  and and_31 (and_31_out, x5, not_93_out, not_94_out, x2, x1);
  and and_32 (and_32_out, x5, not_95_out, x3, not_96_out, x0);
  and and_33 (and_33_out, x5, not_97_out, x3, not_98_out, x1);
  and and_34 (and_34_out, x5, not_99_out, x3, x2, not_100_out);
  and and_35 (and_35_out, x5, not_101_out, x3, x2, not_102_out);
  and and_36 (and_36_out, x5, x4, not_103_out, not_104_out, x0);
  and and_37 (and_37_out, x5, x4, not_105_out, not_106_out, x1);
  and and_38 (and_38_out, x5, x4, not_107_out, x2, not_108_out);
  and and_39 (and_39_out, x5, x4, not_109_out, x2, not_110_out);
  and and_40 (and_40_out, x5, x4, x3, not_111_out, not_112_out);
  and and_41 (and_41_out, x5, x4, x3, not_113_out, not_114_out);
  and and_42 (and_42_out, x5, x4, x3, not_115_out, not_116_out);
  and and_43 (and_43_out, not_117_out, not_118_out, not_119_out, not_120_out, not_121_out, x0);
  and and_44 (and_44_out, not_122_out, not_123_out, not_124_out, not_125_out, x1, not_126_out);
  and and_45 (and_45_out, not_127_out, not_128_out, not_129_out, x2, not_130_out, not_131_out);
  and and_46 (and_46_out, not_132_out, not_133_out, not_134_out, x2, x1, x0);
  and and_47 (and_47_out, not_135_out, not_136_out, x3, not_137_out, not_138_out, not_139_out);
  and and_48 (and_48_out, not_140_out, not_141_out, x3, not_142_out, x1, x0);
  and and_49 (and_49_out, not_143_out, not_144_out, x3, x2, not_145_out, x0);
  and and_50 (and_50_out, not_146_out, not_147_out, x3, x2, x1, not_148_out);
  and and_51 (and_51_out, not_149_out, x4, not_150_out, not_151_out, not_152_out, not_153_out);
  and and_52 (and_52_out, not_154_out, x4, not_155_out, not_156_out, x1, x0);
  and and_53 (and_53_out, not_157_out, x4, not_158_out, x2, not_159_out, x0);
  and and_54 (and_54_out, not_160_out, x4, not_161_out, x2, x1, not_162_out);
  and and_55 (and_55_out, not_163_out, x4, x3, not_164_out, not_165_out, x0);
  and and_56 (and_56_out, not_166_out, x4, x3, not_167_out, x1, not_168_out);
  and and_57 (and_57_out, not_169_out, x4, x3, x2, not_170_out, not_171_out);
  and and_58 (and_58_out, not_172_out, x4, x3, x2, x1, x0);
  and and_59 (and_59_out, x5, not_173_out, not_174_out, not_175_out, not_176_out, not_177_out);
  and and_60 (and_60_out, x5, not_178_out, not_179_out, not_180_out, x1, x0);
  and and_61 (and_61_out, x5, not_181_out, not_182_out, x2, not_183_out, x0);
  and and_62 (and_62_out, x5, not_184_out, not_185_out, x2, x1, not_186_out);
  and and_63 (and_63_out, x5, not_187_out, x3, not_188_out, not_189_out, x0);
  and and_64 (and_64_out, x5, not_190_out, x3, not_191_out, x1, not_192_out);
  and and_65 (and_65_out, x5, not_193_out, x3, x2, not_194_out, not_195_out);
  and and_66 (and_66_out, x5, not_196_out, x3, x2, x1, x0);
  and and_67 (and_67_out, x5, x4, not_197_out, not_198_out, not_199_out, x0);
  and and_68 (and_68_out, x5, x4, not_200_out, not_201_out, x1, not_202_out);
  and and_69 (and_69_out, x5, x4, not_203_out, x2, not_204_out, not_205_out);
  and and_70 (and_70_out, x5, x4, not_206_out, x2, x1, x0);
  and and_71 (and_71_out, x5, x4, x3, not_207_out, not_208_out, not_209_out);
  and and_72 (and_72_out, x5, x4, x3, not_210_out, x1, x0);
  and and_73 (and_73_out, x5, x4, x3, x2, not_211_out, x0);
  and and_74 (and_74_out, x5, x4, x3, x2, x1, not_212_out);
  or or_1 (z2, and_2_out, and_3_out, and_4_out, and_5_out, and_6_out, and_7_out, and_8_out, and_9_out, and_10_out, and_11_out, and_12_out, and_13_out, and_14_out, and_15_out, and_16_out);
  or or_2 (z1, and_17_out, and_18_out, and_19_out, and_20_out, and_21_out, and_22_out, and_23_out, and_24_out, and_25_out, and_26_out, and_27_out, and_28_out, and_29_out, and_30_out, and_31_out, and_32_out, and_33_out, and_34_out, and_35_out, and_36_out, and_37_out, and_38_out, and_39_out, and_40_out, and_41_out, and_42_out);
  or or_3 (z0, and_43_out, and_44_out, and_45_out, and_46_out, and_47_out, and_48_out, and_49_out, and_50_out, and_51_out, and_52_out, and_53_out, and_54_out, and_55_out, and_56_out, and_57_out, and_58_out, and_59_out, and_60_out, and_61_out, and_62_out, and_63_out, and_64_out, and_65_out, and_66_out, and_67_out, and_68_out, and_69_out, and_70_out, and_71_out, and_72_out, and_73_out, and_74_out);

  assign BAF = 1'b0;
  assign INV_OP = 1'b1;
  assign z3 = 1'b0;
  assign z4 = 1'b0;
  assign z5 = 1'b0;
endmodule

module op1 (
  input  x0,
  input  x1,
  input  x2,
  input  x3,
  input  x4,
  input  x5,
  input  y0,
  input  y1,
  input  y2,
  input  y3,
  input  y4,
  input  y5,
  output z5,
  output z4,
  output z3,
  output z2,
  output z1,
  output z0,
  output ZF,
  output BAF,
  output INV_OP
);

  wire comparator_1_eq;

  Comparator #(.width(6), .mode("unsigned")) comparator_1 (
    .a({x5, x4, x3, x2, x1, x0}), .b({y5, y4, y3, y2, y1, y0}), .eq(comparator_1_eq));  // open: gt, lt
  buf and_1 (z0, comparator_1_eq);  // AND_Gate

  assign BAF = 1'b0;
  assign INV_OP = 1'b1;
  assign z1 = 1'b0;
  assign z2 = 1'b0;
  assign z3 = 1'b0;
  assign z4 = 1'b0;
  assign z5 = 1'b0;
  assign ZF = 1'b0;
endmodule

module op2 (
  input  x0,
  input  x1,
  input  x2,
  input  x3,
  input  x4,
  input  x5,
  input  y0,
  input  y1,
  input  y2,
  input  y3,
  input  y4,
  input  y5,
  output z5,
  output z4,
  output z3,
  output z2,
  output z1,
  output z0,
  output ZF,
  output BAF,
  output INV_OP
);

  Comparator #(.width(6), .mode("unsigned")) comparator_1 (
    .a({x5, x4, x3, x2, x1, x0}), .b({y5, y4, y3, y2, y1, y0}), .eq(z0));  // open: gt, lt

  assign BAF = 1'b0;
  assign INV_OP = 1'b1;
  assign z1 = 1'b0;
  assign z2 = 1'b0;
  assign z3 = 1'b0;
  assign z4 = 1'b0;
  assign z5 = 1'b0;
  assign ZF = 1'b0;
endmodule

module op3 (
  input  x0,
  input  x1,
  input  x2,
  input  x3,
  input  x4,
  input  x5,
  output z0,
  output z1,
  output z2,
  output z3,
  output z4,
  output z5,
  output BAF,
  output BAF_2,
  output INV_OP
);

  wire mul_1_z0, mul_1_z1, mul_1_z2, mul_1_z3, mul_1_z4, mul_1_z5, mul_2_z0, mul_2_z1, mul_2_z2, mul_2_z3,
       mul_2_z4, mul_2_z5;

  MUL mul_1 (
    .x0(x0), .x1(x1), .x2(x2), .x3(x3), .x4(x4), .x5(x5), .y0(x0), .y1(x1), .y2(x2), .y3(x3), .y4(x4),
    .y5(x5), .z0(mul_1_z0), .z1(mul_1_z1), .z2(mul_1_z2), .z3(mul_1_z3), .z4(mul_1_z4), .z5(mul_1_z5));  // open: ZF, BAF, INV_OP
  MUL mul_2 (
    .x0(mul_1_z0), .x1(mul_1_z1), .x2(mul_1_z2), .x3(mul_1_z3), .x4(mul_1_z4), .x5(mul_1_z5), .y0(x0),
    .y1(x1), .y2(x2), .y3(x3), .y4(x4), .y5(x5), .z0(mul_2_z0), .z1(mul_2_z1), .z2(mul_2_z2), .z3(mul_2_z3),
    .z4(mul_2_z4), .z5(mul_2_z5));  // open: ZF, BAF, INV_OP
  MUL mul_3 (
    .x0(mul_2_z0), .x1(mul_2_z1), .x2(mul_2_z2), .x3(mul_2_z3), .x4(mul_2_z4), .x5(mul_2_z5), .y0(x0),
    .y1(x1), .y2(x2), .y3(x3), .y4(x4), .y5(x5), .z0(z0), .z1(z1), .z2(z2), .z3(z3), .z4(z4), .z5(z5));  // open: ZF, BAF, INV_OP

  assign BAF = 1'b0;
  assign BAF_2 = 1'b0;
  assign INV_OP = 1'b1;
endmodule

module NEG2 (
  input  x5,
  input  x4,
  input  x3,
  input  x2,
  input  x1,
  input  x0,
  output z5,
  output z4,
  output z3,
  output z2,
  output z1,
  output z0,
  output ZF,
  output BAF,
  output INV_OP
);

  not not_1 (z5, x5);
  not not_2 (z4, x4);
  not not_3 (z3, x3);
  not not_4 (z2, x2);
  not not_5 (z1, x1);
  not not_6 (z0, x0);
  and and_1 (ZF, x5, x4, x3, x2, x1, x0);
  and and_2 (BAF, x5, x4, x3, x2, x1, x0);

  assign INV_OP = 1'b1;
endmodule

module op22 (
  input  x0,
  input  x1,
  input  x2,
  input  x3,
  input  x4,
  input  x5,
  input  y0,
  input  y1,
  input  y2,
  input  y3,
  input  y4,
  input  y5,
  output z5,
  output z4,
  output z3,
  output z2,
  output z1,
  output z0,
  output ZF,
  output BAF,
  output INV_OP
);

  wire comparator_1_eq, comparator_2_eq, comparator_3_eq, comparator_4_eq, comparator_5_eq, comparator_6_eq,
       not_1_out, not_2_out, not_3_out, not_4_out, not_5_out, not_6_out;

  not not_1 (not_1_out, y5);
  Comparator #(.width(1)) comparator_1 (.a(x5), .b(not_1_out), .eq(comparator_1_eq));  // open: gt, lt
  not not_2 (not_2_out, y3);
  not not_3 (not_3_out, y4);
  Comparator #(.width(1)) comparator_2 (.a(x3), .b(not_2_out), .eq(comparator_2_eq));  // open: gt, lt
  not not_4 (not_4_out, y2);
  Comparator #(.width(1)) comparator_3 (.a(x4), .b(not_3_out), .eq(comparator_3_eq));  // open: gt, lt
  Comparator #(.width(1)) comparator_4 (.a(x2), .b(not_4_out), .eq(comparator_4_eq));  // open: gt, lt
  not not_5 (not_5_out, y1);
  Comparator #(.width(1)) comparator_5 (.a(x1), .b(not_5_out), .eq(comparator_5_eq));  // open: gt, lt
  not not_6 (not_6_out, y0);
  Comparator #(.width(1)) comparator_6 (.a(x0), .b(not_6_out), .eq(comparator_6_eq));  // open: gt, lt
  and and_1 (z0, comparator_6_eq, comparator_5_eq, comparator_4_eq, comparator_2_eq, comparator_3_eq, comparator_1_eq);

  assign BAF = 1'b0;
  assign INV_OP = 1'b1;
  assign z1 = 1'b0;
  assign z2 = 1'b0;
  assign z3 = 1'b0;
  assign z4 = 1'b0;
  assign z5 = 1'b0;
  assign ZF = 1'b0;
endmodule

module ALU (
  input  [5:0] X,
  input  [4:0] Function,
  input  [5:0] Y,
  output [8:0] Result
);

  wire [8:0] ADD_z0, AND_z0, CMPZ_z0, DEC_s0, DIV_z0, INC_s0, INV_s0, MUL_z0, N0_z0, N1_z0, NEG_z0, NOT_z0,
       op1_z0, op2_z0, Op3_z0, OR_z0, ROL_z0, ROR_z0, SHL_s0, SHR_z0, SUB_z0, VLD_s0, XOR_z0;
  wire [8:8] multiplexer_1_out;

  VLD VLD (
    .a5(X[5]), .a4(X[4]), .a3(X[3]), .a2(X[2]), .a1(X[1]), .a0(X[0]), .s5(VLD_s0[5]), .s4(VLD_s0[4]),
    .s3(VLD_s0[3]), .s2(VLD_s0[2]), .s1(VLD_s0[1]), .s0(VLD_s0[0]), .ZF(VLD_s0[6]), .BAF(VLD_s0[7]),
    .INV_OP(VLD_s0[8]));
  NEG2 NEG (
    .x5(X[5]), .x4(X[4]), .x3(X[3]), .x2(X[2]), .x1(X[1]), .x0(X[0]), .z5(NEG_z0[5]), .z4(NEG_z0[4]),
    .z3(NEG_z0[3]), .z2(NEG_z0[2]), .z1(NEG_z0[1]), .z0(NEG_z0[0]), .ZF(NEG_z0[6]), .BAF(NEG_z0[7]),
    .INV_OP(NEG_z0[8]));
  INC INC (
    .x5(X[5]), .x4(X[4]), .x3(X[3]), .x2(X[2]), .x1(X[1]), .x0(X[0]), .s5(INC_s0[5]), .s4(INC_s0[4]),
    .s3(INC_s0[3]), .s2(INC_s0[2]), .s1(INC_s0[1]), .s0(INC_s0[0]), .ZF(INC_s0[6]), .BAF(INC_s0[7]),
    .INV_OP(INC_s0[8]));
  DEC DEC (
    .x5(X[5]), .x4(X[4]), .x3(X[3]), .x2(X[2]), .x1(X[1]), .x0(X[0]), .s5(DEC_s0[5]), .s4(DEC_s0[4]),
    .s3(DEC_s0[3]), .s2(DEC_s0[2]), .s1(DEC_s0[1]), .s0(DEC_s0[0]), .ZF(DEC_s0[6]), .BAF(DEC_s0[7]),
    .INV_OP(DEC_s0[8]));
  CMPZ CMPZ (
    .x5(X[5]), .x4(X[4]), .x3(X[3]), .x2(X[2]), .x1(X[1]), .x0(X[0]), .z5(CMPZ_z0[5]), .z4(CMPZ_z0[4]),
    .z3(CMPZ_z0[3]), .z2(CMPZ_z0[2]), .z1(CMPZ_z0[1]), .z0(CMPZ_z0[0]), .ZF(CMPZ_z0[6]), .BAF(CMPZ_z0[7]),
    .INV_OP(CMPZ_z0[8]));
  INV INV (
    .x5(X[5]), .x4(X[4]), .x3(X[3]), .x2(X[2]), .x1(X[1]), .x0(X[0]), .s5(INV_s0[5]), .s4(INV_s0[4]),
    .s3(INV_s0[3]), .s2(INV_s0[2]), .s1(INV_s0[1]), .s0(INV_s0[0]), .ZF(INV_s0[6]), .BAF(INV_s0[7]),
    .INV_OP(INV_s0[8]));
  SHL SHL (
    .x5(X[5]), .x4(X[4]), .x3(X[3]), .x2(X[2]), .x1(X[1]), .x0(X[0]), .s5(SHL_s0[5]), .s4(SHL_s0[4]),
    .s3(SHL_s0[3]), .s2(SHL_s0[2]), .s1(SHL_s0[1]), .s0(SHL_s0[0]), .ZF(SHL_s0[6]), .BAF(SHL_s0[7]),
    .INV_OP(SHL_s0[8]));
  SHR SHR (
    .x5(X[5]), .x4(X[4]), .x3(X[3]), .x2(X[2]), .x1(X[1]), .x0(X[0]), .z5(SHR_z0[5]), .z4(SHR_z0[4]),
    .z3(SHR_z0[3]), .z2(SHR_z0[2]), .z1(SHR_z0[1]), .z0(SHR_z0[0]), .ZF(SHR_z0[6]), .BAF(SHR_z0[7]),
    .INV_OP(SHR_z0[8]));
  ROL ROL (
    .x5(X[5]), .x4(X[4]), .x3(X[3]), .x2(X[2]), .x1(X[1]), .x0(X[0]), .z5(ROL_z0[5]), .z4(ROL_z0[4]),
    .z3(ROL_z0[3]), .z2(ROL_z0[2]), .z1(ROL_z0[1]), .z0(ROL_z0[0]), .ZF(ROL_z0[6]), .BAF(ROL_z0[7]),
    .INV_OP(ROL_z0[8]));
  ROR ROR (
    .x5(X[5]), .x4(X[4]), .x3(X[3]), .x2(X[2]), .x1(X[1]), .x0(X[0]), .z5(ROR_z0[5]), .z4(ROR_z0[4]),
    .z3(ROR_z0[3]), .z2(ROR_z0[2]), .z1(ROR_z0[1]), .z0(ROR_z0[0]), .ZF(ROR_z0[6]), .BAF(ROR_z0[7]),
    .INV_OP(ROR_z0[8]));
  NOT NOT (
    .x0(X[0]), .x1(X[1]), .x2(X[2]), .x3(X[3]), .x4(X[4]), .x5(X[5]), .ZF(NOT_z0[7]), .z0(NOT_z0[0]),
    .z1(NOT_z0[1]), .z2(NOT_z0[2]), .z3(NOT_z0[3]), .z4(NOT_z0[4]), .z5(NOT_z0[5]), .BAF(NOT_z0[6]),
    .INV_OP(NOT_z0[8]));
  N1 N1 (
    .x5(X[5]), .x4(X[4]), .x3(X[3]), .x2(X[2]), .x1(X[1]), .x0(X[0]), .z5(N1_z0[5]), .z4(N1_z0[4]),
    .z3(N1_z0[3]), .z2(N1_z0[2]), .z1(N1_z0[1]), .z0(N1_z0[0]), .ZF(N1_z0[6]), .BAF(N1_z0[7]),
    .INV_OP(N1_z0[8]));
  N0 N0 (
    .x5(X[5]), .x4(X[4]), .x3(X[3]), .x2(X[2]), .x1(X[1]), .x0(X[0]), .z5(N0_z0[5]), .z4(N0_z0[4]),
    .z3(N0_z0[3]), .z2(N0_z0[2]), .z1(N0_z0[1]), .z0(N0_z0[0]), .ZF(N0_z0[6]), .BAF(N0_z0[7]),
    .INV_OP(N0_z0[8]));
  ADD ADD (
    .x0(X[0]), .x1(X[1]), .x2(X[2]), .x3(X[3]), .x4(X[4]), .x5(X[5]), .y0(Y[0]), .y1(Y[1]), .y2(Y[2]),
    .y3(Y[3]), .y4(Y[4]), .y5(Y[5]), .ZF(ADD_z0[6]), .z0(ADD_z0[0]), .z1(ADD_z0[1]), .z2(ADD_z0[2]),
    .z3(ADD_z0[3]), .z4(ADD_z0[4]), .z5(ADD_z0[5]), .BAF(ADD_z0[7]), .INV_OP(ADD_z0[8]));
  SUB SUB (
    .x0(X[0]), .x1(X[1]), .x2(X[2]), .x3(X[3]), .x4(X[4]), .x5(X[5]), .y0(Y[0]), .y1(Y[1]), .y2(Y[2]),
    .y3(Y[3]), .y4(Y[4]), .y5(Y[5]), .ZF(SUB_z0[6]), .z0(SUB_z0[0]), .z1(SUB_z0[1]), .z2(SUB_z0[2]),
    .z3(SUB_z0[3]), .z4(SUB_z0[4]), .z5(SUB_z0[5]), .BAF(SUB_z0[7]), .INV_OP(SUB_z0[8]));
  MUL MUL (
    .x0(X[0]), .x1(X[1]), .x2(X[2]), .x3(X[3]), .x4(X[4]), .x5(X[5]), .y0(Y[0]), .y1(Y[1]), .y2(Y[2]),
    .y3(Y[3]), .y4(Y[4]), .y5(Y[5]), .ZF(MUL_z0[6]), .z0(MUL_z0[0]), .z1(MUL_z0[1]), .z2(MUL_z0[2]),
    .z3(MUL_z0[3]), .z4(MUL_z0[4]), .z5(MUL_z0[5]), .BAF(MUL_z0[7]), .INV_OP(MUL_z0[8]));
  DIV DIV (
    .x0(X[0]), .x1(X[1]), .x2(X[2]), .x3(X[3]), .x4(X[4]), .x5(X[5]), .y0(Y[0]), .y1(Y[1]), .y2(Y[2]),
    .y3(Y[3]), .y4(Y[4]), .y5(Y[5]), .ZF(DIV_z0[6]), .z0(DIV_z0[0]), .z1(DIV_z0[1]), .z2(DIV_z0[2]),
    .z3(DIV_z0[3]), .z4(DIV_z0[4]), .z5(DIV_z0[5]), .BAF(DIV_z0[7]), .INV_OP(DIV_z0[8]));
  op1 op1 (
    .x0(X[0]), .x1(X[1]), .x2(X[2]), .x3(X[3]), .x4(X[4]), .x5(X[5]), .y0(Y[0]), .y1(Y[1]), .y2(Y[2]),
    .y3(Y[3]), .y4(Y[4]), .y5(Y[5]), .z5(op1_z0[5]), .z4(op1_z0[4]), .z3(op1_z0[3]), .z2(op1_z0[2]),
    .z1(op1_z0[1]), .z0(op1_z0[0]), .ZF(op1_z0[6]), .BAF(op1_z0[7]), .INV_OP(op1_z0[8]));
  op22 op2 (
    .x0(X[0]), .x1(X[1]), .x2(X[2]), .x3(X[3]), .x4(X[4]), .x5(X[5]), .y0(Y[0]), .y1(Y[1]), .y2(Y[2]),
    .y3(Y[3]), .y4(Y[4]), .y5(Y[5]), .z5(op2_z0[5]), .z4(op2_z0[4]), .z3(op2_z0[3]), .z2(op2_z0[2]),
    .z1(op2_z0[1]), .z0(op2_z0[0]), .ZF(op2_z0[6]), .BAF(op2_z0[7]), .INV_OP(op2_z0[8]));
  op3 Op3 (
    .x0(X[0]), .x1(X[1]), .x2(X[2]), .x3(X[3]), .x4(X[4]), .x5(X[5]), .z0(Op3_z0[0]), .z1(Op3_z0[1]),
    .z2(Op3_z0[2]), .z3(Op3_z0[3]), .z4(Op3_z0[4]), .z5(Op3_z0[5]), .BAF(Op3_z0[6]), .BAF_2(Op3_z0[7]),
    .INV_OP(Op3_z0[8]));
  XOR XOR (
    .x0(X[0]), .x1(X[1]), .x2(X[2]), .x3(X[3]), .x4(X[4]), .x5(X[5]), .y0(Y[0]), .y1(Y[1]), .y2(Y[2]),
    .y3(Y[3]), .y4(Y[4]), .y5(Y[5]), .ZF(XOR_z0[6]), .z0(XOR_z0[0]), .z1(XOR_z0[1]), .z2(XOR_z0[2]),
    .z3(XOR_z0[3]), .z4(XOR_z0[4]), .z5(XOR_z0[5]), .BAF(XOR_z0[7]), .INV_OP(XOR_z0[8]));
  AND AND (
    .x0(X[0]), .x1(X[1]), .x2(X[2]), .x3(X[3]), .x4(X[4]), .x5(X[5]), .y0(Y[0]), .y1(Y[1]), .y2(Y[2]),
    .y3(Y[3]), .y4(Y[4]), .y5(Y[5]), .ZF(AND_z0[6]), .z0(AND_z0[0]), .z1(AND_z0[1]), .z2(AND_z0[2]),
    .z3(AND_z0[3]), .z4(AND_z0[4]), .z5(AND_z0[5]), .BAF(AND_z0[7]), .INV_OP(AND_z0[8]));
  OR OR (
    .x0(X[0]), .x1(X[1]), .x2(X[2]), .x3(X[3]), .x4(X[4]), .x5(X[5]), .y0(Y[0]), .y1(Y[1]), .y2(Y[2]),
    .y3(Y[3]), .y4(Y[4]), .y5(Y[5]), .ZF(OR_z0[6]), .z0(OR_z0[0]), .z1(OR_z0[1]), .z2(OR_z0[2]),
    .z3(OR_z0[3]), .z4(OR_z0[4]), .z5(OR_z0[5]), .BAF(OR_z0[7]), .INV_OP(OR_z0[8]));
  Multiplexer #(.select(5), .width(9)) multiplexer_1 (
    .in0({9{1'b0}}), .in1(VLD_s0), .in2(NEG_z0), .in3(INC_s0), .in4(DEC_s0), .in5(CMPZ_z0), .in6(INV_s0),
    .in7({9{1'b0}}), .in8(SHL_s0), .in9(SHR_z0), .in10(ROL_z0), .in11(ROR_z0), .in12(NOT_z0), .in13(N1_z0),
    .in14(N0_z0), .in15({9{1'b0}}), .in16(ADD_z0), .in17(SUB_z0), .in18(MUL_z0), .in19(DIV_z0),
    .in20({9{1'b0}}), .in21({9{1'b0}}), .in22({9{1'b0}}), .in23({9{1'b0}}), .in24(op1_z0), .in25(op2_z0),
    .in26(Op3_z0), .in27({9{1'b0}}), .in28(XOR_z0), .in29(AND_z0), .in30(OR_z0), .in31({9{1'b0}}),
    .out({multiplexer_1_out[8], Result[7:0]}), .sel(Function), .en(1'b1));
  not not_2 (Result[8], multiplexer_1_out[8]);
endmodule

module test (
);

  ALU alu_1 ();  // open: Function, X, Y, Result
endmodule
