// Logisim project test_CPU.circ as structural Verilog: 4 circuits, main circuit main
module main (
  output [5:0] out_1,
  output [5:0] r0,
  output [5:0] r1,
  output [5:0] r2,
  output [5:0] r3,
  output out_6,
  output [5:0] r4,
  output [5:0] r5,
  output [5:0] r6,
  output [5:0] r7,
  output [2:0] sregsel,
  output [2:0] dregsel,
  output [5:0] out_13,
  output [4:0] aluop,
  output [8:0] FullAluResult,
  output [5:0] Data_in,
  output [5:0] Result,
  output [5:0] dval,
  output [1:0] out_19,
  output [5:0] dbus,
  output [5:0] sbus,
  output INV_OP,
  output irload,
  output dwrite,
  output Zero,
  output Negative,
  output BAF,
  output ZF,
  output out_29,
  output out_30
);

  wire clock_1_out, clock_2_out, clock_3_out, clock_4_out, imload, pcload, pcsel, readwrite;
  wire [1:0] addrsel;
  wire [5:0] IR_CODE, IR_REG, multiplexer_3_out, pc_adder_1_pc_out, register_4_q;

  Clock clock_1 (.out(clock_1_out));
  RAM #(.addrWidth(6), .dataWidth(6), .bus("separate")) ram_1 (
    .addr(out_1), .din(dbus), .data(Data_in), .str(readwrite), .clk(clock_1_out));  // open: sel, ld, clr
  Register #(.width(6)) register_1 (.D(Data_in), .en(irload), .Q(IR_REG), .clk(clock_2_out));  // open: clr
  Clock clock_2 (.out(clock_2_out));
  Multiplexer #(.select(2), .width(6), .enable("false")) multiplexer_1 (
    .in0(register_4_q), .in1(out_13), .in2(sbus), .in3(dbus), .out(out_1), .sel(addrsel));
  Clock clock_3 (.out(clock_3_out));
  Register #(.width(6)) register_2 (.D(IR_REG), .en(irload), .Q(IR_CODE), .clk(clock_2_out));  // open: clr
  Register #(.width(6)) register_3 (.D(Data_in), .en(imload), .Q(out_13), .clk(clock_3_out));  // open: clr
  Multiplexer #(.select(2), .width(6), .enable("false")) multiplexer_2 (
    .in0(out_13), .in1(sbus), .in2(Data_in), .in3(FullAluResult[5:0]), .out(dval), .sel(out_19));
  Multiplexer #(.width(6), .enable("false")) multiplexer_3 (
    .in0(out_13), .in1(pc_adder_1_pc_out), .out(multiplexer_3_out), .sel(pcsel));
  Register #(.width(6)) register_4 (
    .D(multiplexer_3_out), .en(pcload), .Q(register_4_q), .clk(clock_4_out));  // open: clr
  Clock clock_4 (.out(clock_4_out));
  PC_Adder pc_adder_1 (.PC_in(register_4_q), .PC_out(pc_adder_1_pc_out));
  Decode_Logic decode_logic_1 (
    .dregsel(dregsel), .sregsel(sregsel), .aluop(aluop), .irload(irload), .imload(imload), .pcsel(pcsel),
    .readwrite(readwrite), .dwrite(dwrite), .IR_REG(IR_REG), .IR_Code(IR_CODE), .ZF(FullAluResult[6]),
    .BAF(BAF), .pcload(pcload), .addrsel(addrsel), .regsel(out_19));  // open: ALU_OP, out_21, out_20, out_22, out_13, out_16, phase, out_23
  Register_File register_file_1 (
    .dwrite(dwrite), .dval(dval), .dregsel(dregsel), .r0(r0), .r1(r1), .r2(r2), .r3(r3), .r4(r4), .r5(r5),
    .r6(r6), .r7(r7), .dbus(dbus), .Zero(Zero), .Negative(Negative), .sbus(sbus), .sregsel(sregsel));
  ALU alu_1 (.Function(aluop), .X(dbus), .Y(sbus), .Result({FullAluResult[8], BAF, FullAluResult[6:0]}));

  assign FullAluResult[7] = BAF;
  assign INV_OP = FullAluResult[8];
  assign Result = FullAluResult[5:0];
  assign ZF = FullAluResult[6];

  // Other names for the same wires on the sheet: regsel[1:0] = out_19

  // Notes on the sheet:
  //   Register
  //   Values
  //   IR-Reg
  //   Immed
  //   IR-Code
  //   PC
  //   PC Adder
  //   Regs
  //   Decode Logic
  //   Alu
endmodule

module PC_Adder (
  input  [5:0] PC_in,
  output [5:0] PC_out
);

  Adder #(.width(6)) adder_1 (.a(PC_in), .b(6'b000001), .out(PC_out), .cin(1'b0));  // open: cout

  // Notes on the sheet:
  //   PC Adder
endmodule

module Register_File (
  input  dwrite,
  input  [5:0] dval,
  input  [2:0] dregsel,
  input  [2:0] sregsel,
  output [5:0] r0,
  output [5:0] r1,
  output [5:0] r2,
  output [5:0] r3,
  output [5:0] r4,
  output [5:0] r5,
  output [5:0] r6,
  output [5:0] r7,
  output [5:0] dbus,
  output Zero,
  output Negative,
  output [5:0] sbus
);

  wire clock_1_out, demultiplexer_1_out0, demultiplexer_1_out1, demultiplexer_1_out2, demultiplexer_1_out3,
       demultiplexer_1_out4, demultiplexer_1_out5, demultiplexer_1_out6, demultiplexer_1_out7, or_1_out;

  Demultiplexer #(.select(3), .enable("false")) demultiplexer_1 (
    .out0(demultiplexer_1_out0), .out1(demultiplexer_1_out1), .out2(demultiplexer_1_out2),
    .out3(demultiplexer_1_out3), .out4(demultiplexer_1_out4), .out5(demultiplexer_1_out5),
    .out6(demultiplexer_1_out6), .out7(demultiplexer_1_out7), .in(dwrite), .sel(dregsel));
  Clock clock_1 (.out(clock_1_out));
  Register #(.width(6)) register_1 (.D(dval), .en(demultiplexer_1_out0), .Q(r0), .clk(clock_1_out));  // open: clr
  Register #(.width(6)) register_2 (.D(dval), .en(demultiplexer_1_out1), .Q(r1), .clk(clock_1_out));  // open: clr
  Register #(.width(6)) register_3 (.D(dval), .en(demultiplexer_1_out2), .Q(r2), .clk(clock_1_out));  // open: clr
  Register #(.width(6)) register_4 (.D(dval), .en(demultiplexer_1_out3), .Q(r3), .clk(clock_1_out));  // open: clr
  Register #(.width(6)) register_5 (.D(dval), .en(demultiplexer_1_out4), .Q(r4), .clk(clock_1_out));  // open: clr
  Register #(.width(6)) register_6 (.D(dval), .en(demultiplexer_1_out5), .Q(r5), .clk(clock_1_out));  // open: clr
  Register #(.width(6)) register_7 (.D(dval), .en(demultiplexer_1_out6), .Q(r6), .clk(clock_1_out));  // open: clr
  Register #(.width(6)) register_8 (.D(dval), .en(demultiplexer_1_out7), .Q(r7), .clk(clock_1_out));  // open: clr
  Multiplexer #(.select(3), .width(6), .enable("false")) multiplexer_1 (
    .in0(r0), .in1(r1), .in2(r2), .in3(r3), .in4(r4), .in5(r5), .in6(r6), .in7(r7), .out(dbus), .sel(dregsel));
  Multiplexer #(.select(3), .width(6), .enable("false")) multiplexer_2 (
    .in0(r0), .in1(r1), .in2(r2), .in3(r3), .in4(r4), .in5(r5), .in6(r6), .in7(r7), .out(sbus), .sel(sregsel));
  or or_1 (or_1_out, dbus[0], dbus[1], dbus[2], dbus[3], dbus[4], dbus[5]);
  not not_1 (Zero, or_1_out);

  assign Negative = dbus[5];

  // Other names for the same wires on the sheet: drs[2:0] = dregsel

  // Notes on the sheet:
  //   Register File
endmodule

module Decode_Logic (
  input  [5:0] IR_Code,
  input  [5:0] IR_REG,
  input  ZF,
  input  BAF,
  output [2:0] dregsel,
  output [2:0] sregsel,
  output [4:0] aluop,
  output ALU_OP,
  output [1:0] phase,
  output irload,
  output imload,
  output pcsel,
  output [1:0] out_13,
  output pcload,
  output readwrite,
  output [2:0] out_16,
  output [1:0] regsel,
  output dwrite,
  output [1:0] addrsel,
  output out_20,
  output [1:0] out_21,
  output out_22,
  output out_23
);

  wire and_1_out, and_2_out, and_3_out, and_4_out, and_5_out, and_6_out, clock_1_out, multiplexer_1_out,
       multiplexer_8_out, multiplexer_9_out, not_1_out, not_2_out, not_3_out, not_4_out, not_5_out,
       not_6_out, not_7_out, not_8_out, not_9_out, not_10_out, or_1_out, or_2_out, or_3_out;
  wire [1:0] counter_1_q, multiplexer_2_out, multiplexer_4_out, multiplexer_13_out, multiplexer_14_out;

  not not_1 (not_1_out, ZF);
  not not_2 (not_2_out, BAF);
  Multiplexer #(.select(3), .enable("false")) multiplexer_1 (
    .in0(ZF), .in1(not_1_out), .in2(not_2_out), .in3(BAF), .in4(1'b0), .in5(1'b0), .in6(1'b0), .in7(1'b0),
    .out(multiplexer_1_out), .sel(IR_Code[2:0]));
  Multiplexer #(.select(5), .width(2), .enable("false")) multiplexer_2 (
    .in0(2'b00), .in1(2'b10), .in2(2'b00), .in3(2'b01), .in4(2'b00), .in5(2'b00), .in6(2'b00), .in7(2'b00),
    .in8(2'b00), .in9(2'b00), .in10(2'b00), .in11(2'b00), .in12(2'b10), .in13(2'b00), .in14(2'b00),
    .in15(2'b00), .in16(2'b00), .in17(2'b00), .in18(2'b00), .in19(2'b00), .in20(2'b00), .in21(2'b00),
    .in22(2'b00), .in23(2'b00), .in24(2'b00), .in25(2'b00), .in26(2'b00), .in27(2'b00), .in28(2'b00),
    .in29(2'b00), .in30(2'b00), .in31(2'b00), .out(multiplexer_2_out), .sel(IR_Code[4:0]));
  Multiplexer #(.select(2), .enable("false")) multiplexer_3 (
    .in0(1'b1), .in1(1'b0), .in2(1'b0), .in3(1'b0), .out(irload), .sel(out_13));
  not not_3 (not_3_out, IR_Code[4]);
  Multiplexer #(.width(2), .enable("false")) multiplexer_4 (
    .in0(2'b11), .in1(multiplexer_2_out), .out(multiplexer_4_out), .sel(IR_Code[5]));
  or or_1 (or_1_out, IR_Code[4], IR_Code[3]);
  and and_1 (and_1_out, IR_Code[5], not_3_out, IR_Code[3], multiplexer_1_out);
  and and_2 (and_2_out, IR_Code[0], IR_Code[1], IR_Code[2], IR_Code[3]);
  Multiplexer #(.select(2), .width(2), .enable("false")) multiplexer_5 (
    .in0(2'b00), .in1(2'b00), .in2(multiplexer_4_out), .in3(2'b00), .out(regsel), .sel(out_13));
  and and_3 (and_3_out, IR_Code[3], IR_Code[5]);
  and and_4 (and_4_out, or_1_out, IR_Code[5]);
  or or_2 (or_2_out, and_1_out, and_2_out);
  Multiplexer #(.select(2), .enable("false")) multiplexer_6 (
    .in0(1'b0), .in1(and_3_out), .in2(1'b0), .in3(1'b0), .out(imload), .sel(out_13));
  Multiplexer #(.select(2), .enable("false")) multiplexer_7 (
    .in0(1'b1), .in1(and_4_out), .in2(or_2_out), .in3(1'b0), .out(pcload), .sel(out_13));
  Multiplexer #(.select(5), .enable("false")) multiplexer_8 (
    .in0(1'b0), .in1(1'b1), .in2(1'b0), .in3(1'b1), .in4(1'b0), .in5(1'b0), .in6(1'b0), .in7(1'b0),
    .in8(1'b0), .in9(1'b0), .in10(1'b0), .in11(1'b0), .in12(1'b1), .in13(1'b0), .in14(1'b1), .in15(1'b0),
    .in16(1'b0), .in17(1'b0), .in18(1'b0), .in19(1'b0), .in20(1'b0), .in21(1'b0), .in22(1'b0), .in23(1'b0),
    .in24(1'b0), .in25(1'b0), .in26(1'b0), .in27(1'b0), .in28(1'b0), .in29(1'b0), .in30(1'b0), .in31(1'b0),
    .out(multiplexer_8_out), .sel(IR_Code[4:0]));
  Multiplexer #(.enable("false")) multiplexer_9 (
    .in0(1'b1), .in1(multiplexer_8_out), .out(multiplexer_9_out), .sel(IR_Code[5]));
  Counter #(.width(2), .max('h3)) counter_1 (.Q(counter_1_q), .clk(clock_1_out));  // open: load, D, count, carry, clr
  Clock clock_1 (.out(clock_1_out));
  Multiplexer #(.select(2), .enable("false")) multiplexer_10 (
    .in0(1'b1), .in1(1'b1), .in2(1'b0), .in3(1'b0), .out(pcsel), .sel(out_13));
  not not_4 (not_4_out, IR_Code[0]);
  not not_5 (not_5_out, IR_Code[2]);
  not not_6 (not_6_out, IR_Code[3]);
  not not_7 (not_7_out, IR_Code[4]);
  not not_8 (not_8_out, IR_Code[1]);
  not not_9 (not_9_out, IR_Code[4]);
  Multiplexer #(.select(2), .enable("false")) multiplexer_11 (
    .in0(1'b0), .in1(1'b0), .in2(multiplexer_9_out), .in3(1'b0), .out(dwrite), .sel(out_13));
  and and_5 (and_5_out, not_4_out, IR_Code[1], not_5_out, not_6_out, not_7_out, IR_Code[5]);
  and and_6 (and_6_out, IR_Code[0], not_8_out, IR_Code[2], IR_Code[3], not_9_out, IR_Code[5]);
  and and_7 (out_13[1], counter_1_q[0], counter_1_q[1]);
  and and_8 (out_13[0], counter_1_q[1], not_10_out);
  not not_10 (not_10_out, counter_1_q[0]);
  or or_3 (or_3_out, and_5_out, and_6_out);
  Multiplexer #(.select(2), .enable("false")) multiplexer_12 (
    .in0(1'b0), .in1(1'b0), .in2(or_3_out), .in3(1'b0), .out(readwrite), .sel(out_13));
  Multiplexer #(.width(2), .enable("false")) multiplexer_13 (
    .in0(2'b00), .in1(multiplexer_14_out), .out(multiplexer_13_out), .sel(IR_Code[5]));
  Multiplexer #(.select(5), .width(2), .enable("false")) multiplexer_14 (
    .in0(2'b00), .in1(2'b10), .in2(2'b10), .in3(2'b00), .in4(2'b00), .in5(2'b00), .in6(2'b00), .in7(2'b00),
    .in8(2'b00), .in9(2'b00), .in10(2'b00), .in11(2'b00), .in12(2'b01), .in13(2'b01), .in14(2'b00),
    .in15(2'b00), .in16(2'b00), .in17(2'b00), .in18(2'b00), .in19(2'b00), .in20(2'b00), .in21(2'b00),
    .in22(2'b00), .in23(2'b00), .in24(2'b00), .in25(2'b00), .in26(2'b00), .in27(2'b00), .in28(2'b00),
    .in29(2'b00), .in30(2'b00), .in31(2'b00), .out(multiplexer_14_out), .sel(IR_Code[4:0]));
  Multiplexer #(.select(2), .width(2), .enable("false")) multiplexer_15 (
    .in0(2'b00), .in1(2'b00), .in2(multiplexer_13_out), .in3(2'b00), .out(addrsel), .sel(out_13));

  assign ALU_OP = IR_Code[5];
  assign aluop = IR_Code[4:0];
  assign dregsel = IR_REG[5:3];
  assign out_16 = IR_Code[2:0];
  assign out_20 = IR_Code[5];
  assign out_21 = out_13;
  assign out_22 = IR_Code[5];
  assign out_23 = IR_Code[5];
  assign phase = out_13;
  assign sregsel = IR_REG[2:0];

  // Other names for the same wires on the sheet: irbit9 = IR_Code[5]; op1[2:0] = IR_Code[5:3]; irbit4 = IR_Code[0];
  //   op1op2[4:0] = IR_Code[4:0]; op2[2:0] = IR_Code[2:0]; irbit5 = IR_Code[1]; irbit6 = IR_Code[2];
  //   irbit7 = IR_Code[3]; irbit8 = IR_Code[4]; rd[2:0] = IR_REG[5:3]; rs[2:0] = IR_REG[2:0]

  // Notes on the sheet:
  //   IR Load
  //   PC Load
  //   Register Select
  //   Immed Load
  //   Decode Logic
  //   Phase
  //   Counter
  //   PC Select
  //   Dest Reg Write
  //   Read/Write
  //   Address Select
endmodule
